// Logisim project 2to1单刀双掷.circ as structural Verilog: 1 circuit, main circuit 2to1单刀双掷
// 2to1
module \_2to1单刀双掷  (
  input  \控制信号 ,
  input  \输入1 ,
  input  \输入2 ,
  output \控制1输入1 ,
  output \控制0输入2 
);

  wire inverter_1_output;

  Inverter inverter_1 (.Input(\控制信号 ), .Output(inverter_1_output));
  \传输门  \u_传输门_1  (.\时钟输入 (\控制信号 ), .\输入 (\输入1 ), .\输出 (\控制1输入1 ));
  \传输门  \u_传输门_2  (.\时钟输入 (inverter_1_output), .\输入 (\输入2 ), .\输出 (\控制0输入2 ));
endmodule
