// Logisim project 4位与门.circ as structural Verilog: 1 circuit, main circuit 4位与门
module \_4位与门  (
  input  \第一位输入 ,
  input  \第二位输入 ,
  input  \第三位输入 ,
  input  \第四位输入 ,
  output \输出 
);

  wire and_gate_1_output, and_gate_2_output;

  AND_Gate and_gate_1 (.Input1(\第一位输入 ), .Input2(\第二位输入 ), .Output(and_gate_1_output));
  AND_Gate and_gate_2 (.Input1(\第三位输入 ), .Input2(\第四位输入 ), .Output(and_gate_2_output));
  AND_Gate and_gate_3 (.Input1(and_gate_1_output), .Input2(and_gate_2_output), .Output(\输出 ));
endmodule
