// Logisim project 8位2to1单刀双掷.circ as structural Verilog: 1 circuit, main circuit 8位单刀双掷开关
module \_8位单刀双掷开关  (
  input  \控制信号 ,
  input  in_2,
  input  in_3,
  input  in_4,
  input  in_5,
  input  in_6,
  input  in_7,
  input  in_8,
  input  in_9,
  output out_10,
  output out_11,
  output out_12,
  output out_13,
  output out_14,
  output out_15,
  output out_16,
  output out_17
);

  \_2to1单刀双掷  \u_2to1单刀双掷_1  (.\控制信号 (\控制信号 ), .\输入1 (1'b0), .\输入2 (in_2), .\控制1输入1 (out_10), .\控制0输入2 (out_10));
  \_2to1单刀双掷  \u_2to1单刀双掷_2  (.\控制信号 (\控制信号 ), .\输入1 (1'b0), .\输入2 (in_3), .\控制1输入1 (out_11), .\控制0输入2 (out_11));
  \_2to1单刀双掷  \u_2to1单刀双掷_3  (.\控制信号 (\控制信号 ), .\输入1 (1'b0), .\输入2 (in_4), .\控制1输入1 (out_12), .\控制0输入2 (out_12));
  \_2to1单刀双掷  \u_2to1单刀双掷_4  (.\控制信号 (\控制信号 ), .\输入1 (1'b0), .\输入2 (in_5), .\控制1输入1 (out_13), .\控制0输入2 (out_13));
  \_2to1单刀双掷  \u_2to1单刀双掷_5  (.\控制信号 (\控制信号 ), .\输入1 (1'b0), .\输入2 (in_6), .\控制1输入1 (out_14), .\控制0输入2 (out_14));
  \_2to1单刀双掷  \u_2to1单刀双掷_6  (.\控制信号 (\控制信号 ), .\输入1 (1'b0), .\输入2 (in_7), .\控制1输入1 (out_15), .\控制0输入2 (out_15));
  \_2to1单刀双掷  \u_2to1单刀双掷_7  (.\控制信号 (\控制信号 ), .\输入1 (1'b0), .\输入2 (in_8), .\控制1输入1 (out_16), .\控制0输入2 (out_16));
  \_2to1单刀双掷  \u_2to1单刀双掷_8  (.\控制信号 (\控制信号 ), .\输入1 (1'b0), .\输入2 (in_9), .\控制1输入1 (out_17), .\控制0输入2 (out_17));
endmodule
