// Logisim project 8位或门.circ as structural Verilog: 1 circuit, main circuit 8位或门
module \_8位或门  (
  input  in_1,
  input  in_2,
  input  in_3,
  input  in_4,
  input  in_5,
  input  in_6,
  input  in_7,
  input  in_8,
  output out_9
);

  wire or_gate_1_output, or_gate_2_output, or_gate_3_output, or_gate_4_output, or_gate_5_output,
       or_gate_7_output;

  OR_Gate or_gate_1 (.Input1(in_1), .Input2(in_2), .Output(or_gate_1_output));
  OR_Gate or_gate_2 (.Input1(in_3), .Input2(in_4), .Output(or_gate_2_output));
  OR_Gate or_gate_3 (.Input1(in_5), .Input2(in_6), .Output(or_gate_3_output));
  OR_Gate or_gate_4 (.Input1(in_7), .Input2(in_8), .Output(or_gate_4_output));
  OR_Gate or_gate_5 (.Input1(or_gate_1_output), .Input2(or_gate_2_output), .Output(or_gate_5_output));
  OR_Gate or_gate_6 (.Input1(or_gate_5_output), .Input2(or_gate_7_output), .Output(out_9));
  OR_Gate or_gate_7 (.Input1(or_gate_3_output), .Input2(or_gate_4_output), .Output(or_gate_7_output));
endmodule
