// Logisim project AND_Gate.circ as structural Verilog: 1 circuit, main circuit AND_Gate
// AND
module AND_Gate (
  input  Input1,
  input  Input2,
  output Output
);

  wire transistor_1_out;

  Transistor #(.\type ("n")) transistor_1 (.in(1'b1), .out(transistor_1_out), .gate(Input1));
  Transistor #(.\type ("n")) transistor_2 (.in(transistor_1_out), .out(Output), .gate(Input2));
  Transistor transistor_3 (.in(1'b0), .out(Output), .gate(Input2));
  Transistor transistor_4 (.in(1'b0), .out(Output), .gate(Input1));
endmodule
