// Logisim project Inverters.circ as structural Verilog: 1 circuit, main circuit Inverter
// Not
module Inverter (
  input  Input,
  output Output
);

  Transistor transistor_1 (.in(1'b1), .out(Output), .gate(Input));
  Transistor #(.\type ("n")) transistor_2 (.in(1'b0), .out(Output), .gate(Input));
endmodule
