// Logisim project NAND_Gate.circ as structural Verilog: 1 circuit, main circuit NAND_Gate
// NAND
module NAND_Gate (
  input  Input1,
  input  Input2,
  output Output
);

  wire transistor_4_out;

  Transistor transistor_1 (.in(1'b1), .out(Output), .gate(Input2));
  Transistor transistor_2 (.in(1'b1), .out(Output), .gate(Input1));
  Transistor #(.\type ("n")) transistor_3 (.in(transistor_4_out), .out(Output), .gate(Input1));
  Transistor #(.\type ("n")) transistor_4 (.in(1'b0), .out(transistor_4_out), .gate(Input2));
endmodule
