// Logisim project NOR_Gate.circ as structural Verilog: 1 circuit, main circuit NOR_Gate
// NOR
module NOR_Gate (
  input  Input1,
  input  Input2,
  output Output
);

  wire transistor_1_out;

  Transistor transistor_1 (.in(1'b1), .out(transistor_1_out), .gate(Input1));
  Transistor transistor_2 (.in(transistor_1_out), .out(Output), .gate(Input2));
  Transistor #(.\type ("n")) transistor_3 (.in(1'b0), .out(Output), .gate(Input1));
  Transistor #(.\type ("n")) transistor_4 (.in(1'b0), .out(Output), .gate(Input2));

  // Notes on the sheet:
  //   N型
  //   P型
  //   P型
  //   N型
endmodule
