// Logisim project OR_Gate.circ as structural Verilog: 1 circuit, main circuit OR_Gate
// OR
module OR_Gate (
  input  Input1,
  input  Input2,
  output Output
);

  wire transistor_3_out;

  Transistor #(.\type ("n")) transistor_1 (.in(1'b1), .out(Output), .gate(Input1));
  Transistor transistor_2 (.in(transistor_3_out), .out(Output), .gate(Input1));
  Transistor transistor_3 (.in(1'b0), .out(transistor_3_out), .gate(Input2));
  Transistor #(.\type ("n")) transistor_4 (.in(1'b1), .out(Output), .gate(Input2));

  // Other names for the same wires on the sheet: A = Input2
endmodule
