// Logisim project XOR_Gate.circ as structural Verilog: 1 circuit, main circuit XOR_Gate
// XOR
module XOR_Gate (
  input  Input1,
  input  Input2,
  output Output
);

  wire and_gate_1_output, and_gate_2_output, inverter_1_output, inverter_2_output;

  AND_Gate and_gate_1 (.Input1(Input1), .Input2(inverter_1_output), .Output(and_gate_1_output));
  Inverter inverter_1 (.Input(Input2), .Output(inverter_1_output));
  Inverter inverter_2 (.Input(Input1), .Output(inverter_2_output));
  AND_Gate and_gate_2 (.Input1(inverter_2_output), .Input2(Input2), .Output(and_gate_2_output));
  OR_Gate or_gate_1 (.Input1(and_gate_1_output), .Input2(and_gate_2_output), .Output(Output));
endmodule
