// Logisim project 单刀双掷开关.circ as structural Verilog: 1 circuit, main circuit 单刀双掷开关
// 单刀双支开关
module \单刀双掷开关  (
  input  \输入 ,
  input  \控制信号 ,
  output \控制1 ,
  output \控制0 
);

  wire inverter_1_output;

  Inverter inverter_1 (.Input(\控制信号 ), .Output(inverter_1_output));
  \传输门  \u_传输门_1  (.\时钟输入 (\控制信号 ), .\输入 (\输入 ), .\输出 (\控制1 ));
  \传输门  \u_传输门_2  (.\时钟输入 (inverter_1_output), .\输入 (\输入 ), .\输出 (\控制0 ));
endmodule
