// Logisim project 全加器.circ as structural Verilog: 1 circuit, main circuit 全加器
module \全加器  (
  input  \加数1 ,
  input  \加数2 ,
  input  \上一位的进位 ,
  output \进位 ,
  output \本位的和 
);

  wire \半加器_1_原位 , \半加器_1_进位 , \半加器_2_进位 ;

  \半加器  \u_半加器_1  (.\第一个数的末位 (\加数1 ), .\第二个数的末位 (\加数2 ), .\进位 (\半加器_1_进位 ), .\原位 (\半加器_1_原位 ));
  \半加器  \u_半加器_2  (.\第一个数的末位 (\半加器_1_原位 ), .\第二个数的末位 (\上一位的进位 ), .\进位 (\半加器_2_进位 ), .\原位 (\本位的和 ));
  \半加器  \u_半加器_3  (.\第一个数的末位 (\半加器_1_进位 ), .\第二个数的末位 (\半加器_2_进位 ), .\原位 (\进位 ));  // open: 进位
endmodule
