// Logisim project 八位数减法器.circ as structural Verilog: 1 circuit, main circuit 八位数减法器
module \八位数减法器  (
  input  \被减数的第1位 ,
  input  \被减数的第2位 ,
  input  \被减数的第3位 ,
  input  \被减数的第4位 ,
  input  \被减数的第5位 ,
  input  \被减数的第6位 ,
  input  \被减数的第7位 ,
  input  \被减数的第8位 ,
  input  \减数的第1位 ,
  input  \减数的第2位 ,
  input  \减数的第3位 ,
  input  \减数的第4位 ,
  input  \减数的第5位 ,
  input  \减数的第6位 ,
  input  \减数的第7位 ,
  input  \减数的第8位 ,
  output out_17,
  output out_18,
  output out_19,
  output out_20,
  output out_21,
  output out_22,
  output out_23,
  output out_24,
  output \borrow_0表示有借位 
);

  wire inverter_1_output, \n8位或门_1_out_9 , \twocomplement_1_输出的第1位 , \twocomplement_1_输出的第2位 ,
       \twocomplement_1_输出的第3位 , \twocomplement_1_输出的第4位 , \twocomplement_1_输出的第5位 ,
       \twocomplement_1_输出的第6位 , \twocomplement_1_输出的第7位 , \twocomplement_1_输出的第8位 , \八位数加法器_1_cout ;

  TwoComplement twocomplement_1 (
    .\输入的第1位 (\减数的第1位 ), .\输入的第2位 (\减数的第2位 ), .\输入的第3位 (\减数的第3位 ), .\输入的第4位 (\减数的第4位 ), .\输入的第5位 (\减数的第5位 ),
    .\输入的第6位 (\减数的第6位 ), .\输入的第7位 (\减数的第7位 ), .\输入的第8位 (\减数的第8位 ), .\输出的第1位 (\twocomplement_1_输出的第1位 ),
    .\输出的第2位 (\twocomplement_1_输出的第2位 ), .\输出的第3位 (\twocomplement_1_输出的第3位 ),
    .\输出的第4位 (\twocomplement_1_输出的第4位 ), .\输出的第5位 (\twocomplement_1_输出的第5位 ),
    .\输出的第6位 (\twocomplement_1_输出的第6位 ), .\输出的第7位 (\twocomplement_1_输出的第7位 ),
    .\输出的第8位 (\twocomplement_1_输出的第8位 ));
  \八位数加法器  \u_八位数加法器_1  (
    .\加数1的第1位 (\被减数的第1位 ), .\加数1的第2位 (\被减数的第2位 ), .\加数1的第3位 (\被减数的第3位 ), .\加数1的第4位 (\被减数的第4位 ),
    .\加数1的第5位 (\被减数的第5位 ), .\加数1的第6位 (\被减数的第6位 ), .\加数1的第7位 (\被减数的第7位 ), .\加数1的第8位 (\被减数的第8位 ),
    .\加数2的第1位 (\twocomplement_1_输出的第1位 ), .\加数2的第2位 (\twocomplement_1_输出的第2位 ),
    .\加数2的第3位 (\twocomplement_1_输出的第3位 ), .\加数2的第4位 (\twocomplement_1_输出的第4位 ),
    .\加数2的第5位 (\twocomplement_1_输出的第5位 ), .\加数2的第6位 (\twocomplement_1_输出的第6位 ),
    .\加数2的第7位 (\twocomplement_1_输出的第7位 ), .\加数2的第8位 (\twocomplement_1_输出的第8位 ), .out_17(out_17),
    .out_18(out_18), .out_19(out_19), .out_20(out_20), .out_21(out_21), .out_22(out_22), .out_23(out_23),
    .out_24(out_24), .cout(\八位数加法器_1_cout ));
  \_8位或门  \u_8位或门_1  (
    .in_1(\twocomplement_1_输出的第1位 ), .in_2(\twocomplement_1_输出的第2位 ), .in_3(\twocomplement_1_输出的第3位 ),
    .in_4(\twocomplement_1_输出的第4位 ), .in_5(\twocomplement_1_输出的第5位 ), .in_6(\twocomplement_1_输出的第6位 ),
    .in_7(\twocomplement_1_输出的第7位 ), .in_8(\twocomplement_1_输出的第8位 ), .out_9(\n8位或门_1_out_9 ));
  Inverter inverter_1 (.Input(\n8位或门_1_out_9 ), .Output(inverter_1_output));
  OR_Gate or_gate_1 (.Input1(\八位数加法器_1_cout ), .Input2(inverter_1_output), .Output(\borrow_0表示有借位 ));
endmodule
