// Logisim project 八位数加法器.circ as structural Verilog: 1 circuit, main circuit 八位数加法器
module \八位数加法器  (
  input  \加数1的第1位 ,
  input  \加数1的第2位 ,
  input  \加数1的第3位 ,
  input  \加数1的第4位 ,
  input  \加数1的第5位 ,
  input  \加数1的第6位 ,
  input  \加数1的第7位 ,
  input  \加数1的第8位 ,
  input  \加数2的第1位 ,
  input  \加数2的第2位 ,
  input  \加数2的第3位 ,
  input  \加数2的第4位 ,
  input  \加数2的第5位 ,
  input  \加数2的第6位 ,
  input  \加数2的第7位 ,
  input  \加数2的第8位 ,
  output out_17,
  output out_18,
  output out_19,
  output out_20,
  output out_21,
  output out_22,
  output out_23,
  output out_24,
  output cout
);

  wire \全加器_1_进位 , \全加器_2_进位 , \全加器_3_进位 , \全加器_4_进位 , \全加器_5_进位 , \全加器_6_进位 , \半加器_1_进位 ;

  \全加器  \u_全加器_1  (.\加数1 (\加数1的第7位 ), .\加数2 (\加数2的第7位 ), .\上一位的进位 (\半加器_1_进位 ), .\进位 (\全加器_1_进位 ), .\本位的和 (out_23));
  \半加器  \u_半加器_1  (.\第一个数的末位 (\加数1的第8位 ), .\第二个数的末位 (\加数2的第8位 ), .\进位 (\半加器_1_进位 ), .\原位 (out_24));
  \全加器  \u_全加器_2  (.\加数1 (\加数1的第6位 ), .\加数2 (\加数2的第6位 ), .\上一位的进位 (\全加器_1_进位 ), .\进位 (\全加器_2_进位 ), .\本位的和 (out_22));
  \全加器  \u_全加器_3  (.\加数1 (\加数1的第5位 ), .\加数2 (\加数2的第5位 ), .\上一位的进位 (\全加器_2_进位 ), .\进位 (\全加器_3_进位 ), .\本位的和 (out_21));
  \全加器  \u_全加器_4  (.\加数1 (\加数1的第3位 ), .\加数2 (\加数2的第3位 ), .\上一位的进位 (\全加器_5_进位 ), .\进位 (\全加器_4_进位 ), .\本位的和 (out_19));
  \全加器  \u_全加器_5  (.\加数1 (\加数1的第4位 ), .\加数2 (\加数2的第4位 ), .\上一位的进位 (\全加器_3_进位 ), .\进位 (\全加器_5_进位 ), .\本位的和 (out_20));
  \全加器  \u_全加器_6  (.\加数1 (\加数1的第2位 ), .\加数2 (\加数2的第2位 ), .\上一位的进位 (\全加器_4_进位 ), .\进位 (\全加器_6_进位 ), .\本位的和 (out_18));
  \全加器  \u_全加器_7  (.\加数1 (\加数1的第1位 ), .\加数2 (\加数2的第1位 ), .\上一位的进位 (\全加器_6_进位 ), .\进位 (cout), .\本位的和 (out_17));
endmodule
