// Logisim project 半加器.circ as structural Verilog: 1 circuit, main circuit 半加器
module \半加器  (
  input  \第一个数的末位 ,
  input  \第二个数的末位 ,
  output \进位 ,
  output \原位 
);

  AND_Gate and_gate_1 (.Input1(\第一个数的末位 ), .Input2(\第二个数的末位 ), .Output(\进位 ));
  XOR_Gate xor_gate_1 (.Input1(\第一个数的末位 ), .Input2(\第二个数的末位 ), .Output(\原位 ));
endmodule
