// Logisim project 取补器(TwoComplement).circ as structural Verilog: 1 circuit, main circuit TwoComplement
// 取补器
module TwoComplement (
  input  \输入的第1位 ,
  input  \输入的第2位 ,
  input  \输入的第3位 ,
  input  \输入的第4位 ,
  input  \输入的第5位 ,
  input  \输入的第6位 ,
  input  \输入的第7位 ,
  input  \输入的第8位 ,
  output \输出的第1位 ,
  output \输出的第2位 ,
  output \输出的第3位 ,
  output \输出的第4位 ,
  output \输出的第5位 ,
  output \输出的第6位 ,
  output \输出的第7位 ,
  output \输出的第8位 
);

  wire inverter_1_output, inverter_2_output, inverter_3_output, inverter_4_output, inverter_5_output,
       inverter_6_output, inverter_7_output, inverter_8_output;

  Inverter inverter_1 (.Input(\输入的第1位 ), .Output(inverter_1_output));
  Inverter inverter_2 (.Input(\输入的第2位 ), .Output(inverter_2_output));
  Inverter inverter_3 (.Input(\输入的第3位 ), .Output(inverter_3_output));
  Inverter inverter_4 (.Input(\输入的第4位 ), .Output(inverter_4_output));
  Inverter inverter_5 (.Input(\输入的第5位 ), .Output(inverter_5_output));
  Inverter inverter_6 (.Input(\输入的第6位 ), .Output(inverter_6_output));
  Inverter inverter_7 (.Input(\输入的第7位 ), .Output(inverter_7_output));
  Inverter inverter_8 (.Input(\输入的第8位 ), .Output(inverter_8_output));
  \八位数加法器  \u_八位数加法器_1  (
    .\加数1的第1位 (inverter_1_output), .\加数1的第2位 (inverter_2_output), .\加数1的第3位 (inverter_3_output),
    .\加数1的第4位 (inverter_4_output), .\加数1的第5位 (inverter_5_output), .\加数1的第6位 (inverter_6_output),
    .\加数1的第7位 (inverter_7_output), .\加数1的第8位 (inverter_8_output), .\加数2的第1位 (1'b0), .\加数2的第2位 (1'b0),
    .\加数2的第3位 (1'b0), .\加数2的第4位 (1'b0), .\加数2的第5位 (1'b0), .\加数2的第6位 (1'b0), .\加数2的第7位 (1'b0),
    .\加数2的第8位 (1'b1), .out_17(\输出的第1位 ), .out_18(\输出的第2位 ), .out_19(\输出的第3位 ), .out_20(\输出的第4位 ),
    .out_21(\输出的第5位 ), .out_22(\输出的第6位 ), .out_23(\输出的第7位 ), .out_24(\输出的第8位 ));  // open: cout
endmodule
