// Logisim project 四位加法器.circ as structural Verilog: 1 circuit, main circuit 四位加法器
module \四位加法器  (
  input  \数字1的第四位 ,
  input  \数字1的第三位 ,
  input  \数字1的第二位 ,
  input  \数字1的第一位 ,
  input  \数字2的第四位 ,
  input  \数字2的第三位 ,
  input  \数字2的第二位 ,
  input  \数字2的第一位 ,
  output \输出的第四位 ,
  output \输出的第三位 ,
  output \输出的第二位 ,
  output \输出的第一位 
);

  wire \全加器_1_进位 , \全加器_3_进位 , \半加器_1_进位 ;

  \半加器  \u_半加器_1  (.\第一个数的末位 (\数字1的第一位 ), .\第二个数的末位 (\数字2的第一位 ), .\进位 (\半加器_1_进位 ), .\原位 (\输出的第一位 ));
  \全加器  \u_全加器_1  (.\加数1 (\数字1的第二位 ), .\加数2 (\数字2的第二位 ), .\上一位的进位 (\半加器_1_进位 ), .\进位 (\全加器_1_进位 ), .\本位的和 (\输出的第二位 ));
  \全加器  \u_全加器_2  (.\加数1 (\数字1的第四位 ), .\加数2 (\数字2的第四位 ), .\上一位的进位 (\全加器_3_进位 ), .\本位的和 (\输出的第四位 ));  // open: 进位
  \全加器  \u_全加器_3  (.\加数1 (\数字1的第三位 ), .\加数2 (\数字2的第三位 ), .\上一位的进位 (\全加器_1_进位 ), .\进位 (\全加器_3_进位 ), .\本位的和 (\输出的第三位 ));
endmodule
