// Logisim project 递减器.circ as structural Verilog: 1 circuit, main circuit 递减器
module \递减器  (
  input  in_1,
  input  in_2,
  input  in_3,
  input  in_4,
  input  in_5,
  input  in_6,
  input  in_7,
  input  in_8,
  output out_9,
  output out_10,
  output out_11,
  output out_12,
  output out_13,
  output out_14,
  output out_15,
  output out_16
);

  \八位数减法器  \u_八位数减法器_1  (
    .\被减数的第1位 (in_1), .\被减数的第2位 (in_2), .\被减数的第3位 (in_3), .\被减数的第4位 (in_4), .\被减数的第5位 (in_5),
    .\被减数的第6位 (in_6), .\被减数的第7位 (in_7), .\被减数的第8位 (in_8), .\减数的第1位 (1'b0), .\减数的第2位 (1'b0), .\减数的第3位 (1'b0),
    .\减数的第4位 (1'b0), .\减数的第5位 (1'b0), .\减数的第6位 (1'b0), .\减数的第7位 (1'b0), .\减数的第8位 (1'b1), .out_17(out_9),
    .out_18(out_10), .out_19(out_11), .out_20(out_12), .out_21(out_13), .out_22(out_14), .out_23(out_15),
    .out_24(out_16));  // open: borrow_0表示有借位
endmodule
