// Logisim project 递增器.circ as structural Verilog: 1 circuit, main circuit 递增器
module \递增器  (
  input  in_1,
  input  in_2,
  input  in_3,
  input  in_4,
  input  in_5,
  input  in_6,
  input  in_7,
  input  in_8,
  output out_9,
  output out_10,
  output out_11,
  output out_12,
  output out_13,
  output out_14,
  output out_15,
  output out_16
);

  \八位数加法器  \u_八位数加法器_1  (
    .\加数1的第1位 (in_1), .\加数1的第2位 (in_2), .\加数1的第3位 (in_3), .\加数1的第4位 (in_4), .\加数1的第5位 (in_5),
    .\加数1的第6位 (in_6), .\加数1的第7位 (in_7), .\加数1的第8位 (in_8), .\加数2的第1位 (1'b0), .\加数2的第2位 (1'b0),
    .\加数2的第3位 (1'b0), .\加数2的第4位 (1'b0), .\加数2的第5位 (1'b0), .\加数2的第6位 (1'b0), .\加数2的第7位 (1'b0),
    .\加数2的第8位 (1'b1), .out_17(out_9), .out_18(out_10), .out_19(out_11), .out_20(out_12), .out_21(out_13),
    .out_22(out_14), .out_23(out_15), .out_24(out_16));  // open: cout
endmodule
