// Logisim project 八位数按位与.circ as structural Verilog: 1 circuit, main circuit 8位按位与
// 按位与
module \_8位按位与  (
  input  \第1个数的第1位 ,
  input  \第1个数的第2位 ,
  input  \第1个数的第3位 ,
  input  \第1个数的第4位 ,
  input  \第1个数的第5位 ,
  input  \第1个数的第6位 ,
  input  \第1个数的第7位 ,
  input  \第1个数的第8位 ,
  input  \第2个数的第1位 ,
  input  \第2个数的第2位 ,
  input  \第2个数的第3位 ,
  input  \第2个数的第4位 ,
  input  \第2个数的第5位 ,
  input  \第2个数的第6位 ,
  input  \第2个数的第7位 ,
  input  \第2个数的第8位 ,
  output \输出的第1位 ,
  output \输出的第2位 ,
  output \输出的第3位 ,
  output \输出的第4位 ,
  output \输出的第5位 ,
  output \输出的第6位 ,
  output \输出的第7位 ,
  output \输出的第8位 
);

  AND_Gate and_gate_1 (.Input1(\第1个数的第1位 ), .Input2(\第2个数的第1位 ), .Output(\输出的第1位 ));
  AND_Gate and_gate_2 (.Input1(\第1个数的第2位 ), .Input2(\第2个数的第2位 ), .Output(\输出的第2位 ));
  AND_Gate and_gate_3 (.Input1(\第1个数的第3位 ), .Input2(\第2个数的第3位 ), .Output(\输出的第3位 ));
  AND_Gate and_gate_4 (.Input1(\第1个数的第4位 ), .Input2(\第2个数的第4位 ), .Output(\输出的第4位 ));
  AND_Gate and_gate_5 (.Input1(\第1个数的第5位 ), .Input2(\第2个数的第5位 ), .Output(\输出的第5位 ));
  AND_Gate and_gate_6 (.Input1(\第1个数的第6位 ), .Input2(\第2个数的第6位 ), .Output(\输出的第6位 ));
  AND_Gate and_gate_7 (.Input1(\第1个数的第7位 ), .Input2(\第2个数的第7位 ), .Output(\输出的第7位 ));
  AND_Gate and_gate_8 (.Input1(\第1个数的第8位 ), .Input2(\第2个数的第8位 ), .Output(\输出的第8位 ));
endmodule
