// Logisim project 八位数按位非.circ as structural Verilog: 1 circuit, main circuit 8位数按位非
module \_8位数按位非  (
  input  \输入第1位 ,
  input  \输入第2位 ,
  input  \输入第3位 ,
  input  \输入第4位 ,
  input  \输入第5位 ,
  input  \输入第6位 ,
  input  \输入第7位 ,
  input  \输入第8位 ,
  output out_9,
  output out_10,
  output out_11,
  output out_12,
  output out_13,
  output out_14,
  output out_15,
  output out_16
);

  Inverter inverter_1 (.Input(\输入第1位 ), .Output(out_9));
  Inverter inverter_2 (.Input(\输入第2位 ), .Output(out_10));
  Inverter inverter_3 (.Input(\输入第3位 ), .Output(out_11));
  Inverter inverter_4 (.Input(\输入第4位 ), .Output(out_12));
  Inverter inverter_5 (.Input(\输入第5位 ), .Output(out_13));
  Inverter inverter_6 (.Input(\输入第6位 ), .Output(out_14));
  Inverter inverter_7 (.Input(\输入第7位 ), .Output(out_15));
  Inverter inverter_8 (.Input(\输入第8位 ), .Output(out_16));
endmodule
