// Logisim project 右移1位.circ as structural Verilog: 1 circuit, main circuit 右移1位
module \右移1位  (
  input  in_1,
  input  in_2,
  input  in_3,
  input  in_4,
  input  in_5,
  input  in_6,
  input  in_7,
  input  in_8,
  output out_9,
  output out_10,
  output out_11,
  output out_12,
  output out_13,
  output out_14,
  output out_15,
  output out_16
);


  assign out_9 = 1'b0;
  assign out_10 = in_1;
  assign out_11 = in_2;
  assign out_12 = in_3;
  assign out_13 = in_4;
  assign out_14 = in_5;
  assign out_15 = in_6;
  assign out_16 = in_7;
endmodule
