// Logisim project 大于判断.circ as structural Verilog: 1 circuit, main circuit 大于判断
module \大于判断  (
  input  in_1,
  input  in_2,
  input  in_3,
  input  in_4,
  input  in_5,
  input  in_6,
  input  in_7,
  input  in_8,
  input  in_9,
  input  in_10,
  input  in_11,
  input  in_12,
  input  in_13,
  input  in_14,
  input  in_15,
  input  in_16,
  output out_17,
  output out_18,
  output out_19,
  output out_20,
  output out_21,
  output out_22,
  output out_23,
  output out_24
);

  wire \八位数减法器_1_borrow_0表示有借位 ;

  \八位数减法器  \u_八位数减法器_1  (
    .\被减数的第1位 (in_9), .\被减数的第2位 (in_10), .\被减数的第3位 (in_11), .\被减数的第4位 (in_12), .\被减数的第5位 (in_13),
    .\被减数的第6位 (in_14), .\被减数的第7位 (in_15), .\被减数的第8位 (in_16), .\减数的第1位 (in_1), .\减数的第2位 (in_2),
    .\减数的第3位 (in_3), .\减数的第4位 (in_4), .\减数的第5位 (in_5), .\减数的第6位 (in_6), .\减数的第7位 (in_7), .\减数的第8位 (in_8),
    .\borrow_0表示有借位 (\八位数减法器_1_borrow_0表示有借位 ));  // open: out_17, out_18, out_19, out_20, out_21, out_22, out_23, out_24
  Inverter inverter_1 (.Input(\八位数减法器_1_borrow_0表示有借位 ), .Output(out_17));

  assign out_18 = out_17;
  assign out_19 = out_17;
  assign out_20 = out_17;
  assign out_21 = out_17;
  assign out_22 = out_17;
  assign out_23 = out_17;
  assign out_24 = out_17;
endmodule
