// Logisim project 相等判断.circ as structural Verilog: 1 circuit, main circuit 相等判断
// is_equal
module \相等判断  (
  input  in_1,
  input  in_2,
  input  in_3,
  input  in_4,
  input  in_5,
  input  in_6,
  input  in_7,
  input  in_8,
  input  in_9,
  input  in_10,
  input  in_11,
  input  in_12,
  input  in_13,
  input  in_14,
  input  in_15,
  input  in_16,
  output out_17,
  output out_18,
  output out_19,
  output \相等输出1_不相等是0 ,
  output out_21,
  output out_22,
  output out_23,
  output out_24
);

  wire or_gate_1_output, or_gate_2_output, or_gate_3_output, or_gate_4_output, or_gate_5_output,
       or_gate_6_output, or_gate_7_output, xor_gate_1_output, xor_gate_2_output, xor_gate_3_output,
       xor_gate_4_output, xor_gate_5_output, xor_gate_6_output, xor_gate_7_output, xor_gate_8_output;

  XOR_Gate xor_gate_1 (.Input1(in_1), .Input2(in_9), .Output(xor_gate_1_output));
  XOR_Gate xor_gate_2 (.Input1(in_2), .Input2(in_10), .Output(xor_gate_2_output));
  XOR_Gate xor_gate_3 (.Input1(in_3), .Input2(in_11), .Output(xor_gate_3_output));
  XOR_Gate xor_gate_4 (.Input1(in_4), .Input2(in_12), .Output(xor_gate_4_output));
  XOR_Gate xor_gate_5 (.Input1(in_5), .Input2(in_13), .Output(xor_gate_5_output));
  XOR_Gate xor_gate_6 (.Input1(in_6), .Input2(in_14), .Output(xor_gate_6_output));
  XOR_Gate xor_gate_7 (.Input1(in_7), .Input2(in_15), .Output(xor_gate_7_output));
  XOR_Gate xor_gate_8 (.Input1(in_8), .Input2(in_16), .Output(xor_gate_8_output));
  OR_Gate or_gate_1 (.Input1(xor_gate_1_output), .Input2(xor_gate_2_output), .Output(or_gate_1_output));
  OR_Gate or_gate_2 (.Input1(xor_gate_3_output), .Input2(xor_gate_4_output), .Output(or_gate_2_output));
  OR_Gate or_gate_3 (.Input1(xor_gate_5_output), .Input2(xor_gate_6_output), .Output(or_gate_3_output));
  OR_Gate or_gate_4 (.Input1(xor_gate_7_output), .Input2(xor_gate_8_output), .Output(or_gate_4_output));
  OR_Gate or_gate_5 (.Input1(or_gate_1_output), .Input2(or_gate_2_output), .Output(or_gate_5_output));
  OR_Gate or_gate_6 (.Input1(or_gate_3_output), .Input2(or_gate_4_output), .Output(or_gate_6_output));
  OR_Gate or_gate_7 (.Input1(or_gate_5_output), .Input2(or_gate_6_output), .Output(or_gate_7_output));
  Inverter inverter_1 (.Input(or_gate_7_output), .Output(out_17));

  assign out_18 = out_17;
  assign out_19 = out_17;
  assign out_21 = out_17;
  assign out_22 = out_17;
  assign out_23 = out_17;
  assign out_24 = out_17;
  assign \相等输出1_不相等是0  = out_17;
endmodule
