// Logisim project 16选1选择器.circ as structural Verilog: 1 circuit, main circuit 16选1选择器
module \_16选1选择器  (
  input  _0000,
  input  _0001,
  input  _0010,
  input  _0011,
  input  _0100,
  input  _0101,
  input  _0110,
  input  _0111,
  input  _1000,
  input  _1001,
  input  _1010,
  input  _1011,
  input  _1100,
  input  _1101,
  input  _1110,
  input  _1111,
  input  \选择码1 ,
  input  \选择码2 ,
  input  \选择码3 ,
  input  \选择码4 ,
  output out_21
);

  wire \n4选1选择器_1_out_7 , \n4选1选择器_2_out_7 , \n4选1选择器_3_out_7 , \n4选1选择器_4_out_7 ;

  \_4选1选择器  \u_4选1选择器_1  (
    ._00(_0000), ._01(_0100), ._10(_1000), ._11(_1100), .\选择码1 (\选择码1 ), .\选择码2 (\选择码2 ),
    .out_7(\n4选1选择器_1_out_7 ));
  \_4选1选择器  \u_4选1选择器_2  (
    ._00(_0001), ._01(_0101), ._10(_1001), ._11(_1101), .\选择码1 (\选择码1 ), .\选择码2 (\选择码2 ),
    .out_7(\n4选1选择器_2_out_7 ));
  \_4选1选择器  \u_4选1选择器_3  (
    ._00(_0010), ._01(_0110), ._10(_1010), ._11(_1110), .\选择码1 (\选择码1 ), .\选择码2 (\选择码2 ),
    .out_7(\n4选1选择器_3_out_7 ));
  \_4选1选择器  \u_4选1选择器_4  (
    ._00(_0011), ._01(_0111), ._10(_1011), ._11(_1111), .\选择码1 (\选择码1 ), .\选择码2 (\选择码2 ),
    .out_7(\n4选1选择器_4_out_7 ));
  \_4选1选择器  \u_4选1选择器_5  (
    ._00(\n4选1选择器_1_out_7 ), ._01(\n4选1选择器_2_out_7 ), ._10(\n4选1选择器_3_out_7 ), ._11(\n4选1选择器_4_out_7 ),
    .\选择码1 (\选择码3 ), .\选择码2 (\选择码4 ), .out_7(out_21));
endmodule
