// Logisim project 2选1选择器.circ as structural Verilog: 1 circuit, main circuit 2选1选择器
module \_2选1选择器  (
  input  \输入1 ,
  input  \输入2 ,
  input  \选择_1表示输入1_0表示输入2 ,
  output \输出 
);

  wire and_gate_1_output, and_gate_2_output, inverter_1_output;

  AND_Gate and_gate_1 (.Input1(\输入1 ), .Input2(\选择_1表示输入1_0表示输入2 ), .Output(and_gate_1_output));
  Inverter inverter_1 (.Input(\选择_1表示输入1_0表示输入2 ), .Output(inverter_1_output));
  AND_Gate and_gate_2 (.Input1(\输入2 ), .Input2(inverter_1_output), .Output(and_gate_2_output));
  OR_Gate or_gate_1 (.Input1(and_gate_1_output), .Input2(and_gate_2_output), .Output(\输出 ));
endmodule
