// Logisim project 4选1选择器.circ as structural Verilog: 1 circuit, main circuit 4选1选择器
module \_4选1选择器  (
  input  _00,
  input  _01,
  input  _10,
  input  _11,
  input  \选择码1 ,
  input  \选择码2 ,
  output out_7
);

  wire \n2选1选择器_1_输出 , \n2选1选择器_2_输出 ;

  \_2选1选择器  \u_2选1选择器_1  (.\输入1 (_11), .\输入2 (_01), .\选择_1表示输入1_0表示输入2 (\选择码1 ), .\输出 (\n2选1选择器_1_输出 ));
  \_2选1选择器  \u_2选1选择器_2  (.\输入1 (_10), .\输入2 (_00), .\选择_1表示输入1_0表示输入2 (\选择码1 ), .\输出 (\n2选1选择器_2_输出 ));
  \_2选1选择器  \u_2选1选择器_3  (.\输入1 (\n2选1选择器_1_输出 ), .\输入2 (\n2选1选择器_2_输出 ), .\选择_1表示输入1_0表示输入2 (\选择码2 ), .\输出 (out_7));
endmodule
