// Logisim project 8位带宽接口的8位带宽的16选1选择器.circ as structural Verilog: 1 circuit, main circuit 8位接口带宽的16选1选择器
module \_8位接口带宽的16选1选择器  (
  input  [7:0] \第一个8位输入 ,
  input  [7:0] \第二个8位输入 ,
  input  [7:0] \第三个8位输入 ,
  input  [7:0] \第四个8位输入 ,
  input  [7:0] \第五个8位输入 ,
  input  [7:0] \第六个8位输入 ,
  input  [7:0] \第七个8位输入 ,
  input  [7:0] \第八个8位输入 ,
  input  [7:0] \第九个8位输入 ,
  input  [7:0] \第十个8位输入 ,
  input  [7:0] \第11个8位输入 ,
  input  [7:0] \第12个8位输入 ,
  input  [7:0] \第13个8位输入 ,
  input  [7:0] \第14个8位输入 ,
  input  [7:0] \第15个8位输入 ,
  input  [7:0] \第16个8位输入 ,
  input  \控制码1 ,
  input  \控制码2 ,
  input  \控制码3 ,
  input  \控制码4 ,
  output [7:0] out_21
);

  \_8位带宽的16选1选择器  \u_8位带宽的16选1选择器_1  (
    .in_1(\第一个8位输入 [7]), .in_2(\第一个8位输入 [6]), .in_3(\第一个8位输入 [5]), .in_4(\第一个8位输入 [4]), .in_5(\第一个8位输入 [3]),
    .in_6(\第一个8位输入 [2]), .in_7(\第一个8位输入 [1]), .in_8(\第一个8位输入 [0]), .in_9(\第二个8位输入 [7]), .in_10(\第二个8位输入 [6]),
    .in_11(\第二个8位输入 [5]), .in_12(\第二个8位输入 [4]), .in_13(\第二个8位输入 [3]), .in_14(\第二个8位输入 [2]),
    .in_15(\第二个8位输入 [1]), .in_16(\第二个8位输入 [0]), .in_17(\第三个8位输入 [7]), .in_18(\第三个8位输入 [6]),
    .in_19(\第三个8位输入 [5]), .in_20(\第三个8位输入 [4]), .in_21(\第三个8位输入 [3]), .in_22(\第三个8位输入 [2]),
    .in_23(\第三个8位输入 [1]), .in_24(\第三个8位输入 [0]), .in_25(\第四个8位输入 [7]), .in_26(\第四个8位输入 [6]),
    .in_27(\第四个8位输入 [5]), .in_28(\第四个8位输入 [4]), .in_29(\第四个8位输入 [3]), .in_30(\第四个8位输入 [2]),
    .in_31(\第四个8位输入 [1]), .in_32(\第四个8位输入 [0]), .in_33(\第五个8位输入 [7]), .in_34(\第五个8位输入 [6]),
    .in_35(\第五个8位输入 [5]), .in_36(\第五个8位输入 [4]), .in_37(\第五个8位输入 [3]), .in_38(\第五个8位输入 [2]),
    .in_39(\第五个8位输入 [1]), .in_40(\第五个8位输入 [0]), .in_41(\第六个8位输入 [7]), .in_42(\第六个8位输入 [6]),
    .in_43(\第六个8位输入 [5]), .in_44(\第六个8位输入 [4]), .in_45(\第六个8位输入 [3]), .in_46(\第六个8位输入 [2]),
    .in_47(\第六个8位输入 [1]), .in_48(\第六个8位输入 [0]), .in_49(\第七个8位输入 [7]), .in_50(\第七个8位输入 [6]),
    .in_51(\第七个8位输入 [5]), .in_52(\第七个8位输入 [4]), .in_53(\第七个8位输入 [3]), .in_54(\第七个8位输入 [2]),
    .in_55(\第七个8位输入 [1]), .in_56(\第七个8位输入 [0]), .in_57(\第八个8位输入 [7]), .in_58(\第八个8位输入 [6]),
    .in_59(\第八个8位输入 [5]), .in_60(\第八个8位输入 [4]), .in_61(\第八个8位输入 [3]), .in_62(\第八个8位输入 [2]),
    .in_63(\第八个8位输入 [1]), .in_64(\第八个8位输入 [0]), .in_65(\第九个8位输入 [7]), .in_66(\第九个8位输入 [6]),
    .in_67(\第九个8位输入 [5]), .in_68(\第九个8位输入 [4]), .in_69(\第九个8位输入 [3]), .in_70(\第九个8位输入 [2]),
    .in_71(\第九个8位输入 [1]), .in_72(\第九个8位输入 [0]), .in_73(\第十个8位输入 [7]), .in_74(\第十个8位输入 [6]),
    .in_75(\第十个8位输入 [5]), .in_76(\第十个8位输入 [4]), .in_77(\第十个8位输入 [3]), .in_78(\第十个8位输入 [2]),
    .in_79(\第十个8位输入 [1]), .in_80(\第十个8位输入 [0]), .in_81(\第11个8位输入 [7]), .in_82(\第11个8位输入 [6]),
    .in_83(\第11个8位输入 [5]), .in_84(\第11个8位输入 [4]), .in_85(\第11个8位输入 [3]), .in_86(\第11个8位输入 [2]),
    .in_87(\第11个8位输入 [1]), .in_88(\第11个8位输入 [0]), .in_89(\第12个8位输入 [7]), .in_90(\第12个8位输入 [6]),
    .in_91(\第12个8位输入 [5]), .in_92(\第12个8位输入 [4]), .in_93(\第12个8位输入 [3]), .in_94(\第12个8位输入 [2]),
    .in_95(\第12个8位输入 [1]), .in_96(\第12个8位输入 [0]), .in_97(\第13个8位输入 [7]), .in_98(\第13个8位输入 [6]),
    .in_99(\第13个8位输入 [5]), .in_100(\第13个8位输入 [4]), .in_101(\第13个8位输入 [3]), .in_102(\第13个8位输入 [2]),
    .in_103(\第13个8位输入 [1]), .in_104(\第13个8位输入 [0]), .in_105(\第14个8位输入 [7]), .in_106(\第14个8位输入 [6]),
    .in_107(\第14个8位输入 [5]), .in_108(\第14个8位输入 [4]), .in_109(\第14个8位输入 [3]), .in_110(\第14个8位输入 [2]),
    .in_111(\第14个8位输入 [1]), .in_112(\第14个8位输入 [0]), .in_113(\第15个8位输入 [7]), .in_114(\第15个8位输入 [6]),
    .in_115(\第15个8位输入 [5]), .in_116(\第15个8位输入 [4]), .in_117(\第15个8位输入 [3]), .in_118(\第15个8位输入 [2]),
    .in_119(\第15个8位输入 [1]), .in_120(\第15个8位输入 [0]), .in_121(\第16个8位输入 [7]), .in_122(\第16个8位输入 [6]),
    .in_123(\第16个8位输入 [5]), .in_124(\第16个8位输入 [4]), .in_125(\第16个8位输入 [3]), .in_126(\第16个8位输入 [2]),
    .in_127(\第16个8位输入 [1]), .in_128(\第16个8位输入 [0]), .\控制码1 (\控制码1 ), .\控制码2 (\控制码2 ), .\控制码3 (\控制码3 ),
    .\控制码4 (\控制码4 ), .out_133(out_21[7]), .out_134(out_21[6]), .out_135(out_21[5]), .out_136(out_21[4]),
    .out_137(out_21[3]), .out_138(out_21[2]), .out_139(out_21[1]), .out_140(out_21[0]));
endmodule
