// Logisim project 8位带宽的16选1选择器.circ as structural Verilog: 1 circuit, main circuit 8位带宽的16选1选择器
module \_8位带宽的16选1选择器  (
  input  in_1,
  input  in_2,
  input  in_3,
  input  in_4,
  input  in_5,
  input  in_6,
  input  in_7,
  input  in_8,
  input  in_9,
  input  in_10,
  input  in_11,
  input  in_12,
  input  in_13,
  input  in_14,
  input  in_15,
  input  in_16,
  input  in_17,
  input  in_18,
  input  in_19,
  input  in_20,
  input  in_21,
  input  in_22,
  input  in_23,
  input  in_24,
  input  in_25,
  input  in_26,
  input  in_27,
  input  in_28,
  input  in_29,
  input  in_30,
  input  in_31,
  input  in_32,
  input  in_33,
  input  in_34,
  input  in_35,
  input  in_36,
  input  in_37,
  input  in_38,
  input  in_39,
  input  in_40,
  input  in_41,
  input  in_42,
  input  in_43,
  input  in_44,
  input  in_45,
  input  in_46,
  input  in_47,
  input  in_48,
  input  in_49,
  input  in_50,
  input  in_51,
  input  in_52,
  input  in_53,
  input  in_54,
  input  in_55,
  input  in_56,
  input  in_57,
  input  in_58,
  input  in_59,
  input  in_60,
  input  in_61,
  input  in_62,
  input  in_63,
  input  in_64,
  input  in_65,
  input  in_66,
  input  in_67,
  input  in_68,
  input  in_69,
  input  in_70,
  input  in_71,
  input  in_72,
  input  in_73,
  input  in_74,
  input  in_75,
  input  in_76,
  input  in_77,
  input  in_78,
  input  in_79,
  input  in_80,
  input  in_81,
  input  in_82,
  input  in_83,
  input  in_84,
  input  in_85,
  input  in_86,
  input  in_87,
  input  in_88,
  input  in_89,
  input  in_90,
  input  in_91,
  input  in_92,
  input  in_93,
  input  in_94,
  input  in_95,
  input  in_96,
  input  in_97,
  input  in_98,
  input  in_99,
  input  in_100,
  input  in_101,
  input  in_102,
  input  in_103,
  input  in_104,
  input  in_105,
  input  in_106,
  input  in_107,
  input  in_108,
  input  in_109,
  input  in_110,
  input  in_111,
  input  in_112,
  input  in_113,
  input  in_114,
  input  in_115,
  input  in_116,
  input  in_117,
  input  in_118,
  input  in_119,
  input  in_120,
  input  in_121,
  input  in_122,
  input  in_123,
  input  in_124,
  input  in_125,
  input  in_126,
  input  in_127,
  input  in_128,
  input  \控制码1 ,
  input  \控制码2 ,
  input  \控制码3 ,
  input  \控制码4 ,
  output out_133,
  output out_134,
  output out_135,
  output out_136,
  output out_137,
  output out_138,
  output out_139,
  output out_140
);

  \_16选1选择器  \u_16选1选择器_1  (
    ._0000(in_1), ._0001(in_9), ._0010(in_17), ._0011(in_25), ._0100(in_33), ._0101(in_41), ._0110(in_49),
    ._0111(in_57), ._1000(in_65), ._1001(in_73), ._1010(in_81), ._1011(in_89), ._1100(in_97), ._1101(in_105),
    ._1110(in_113), ._1111(in_121), .\选择码1 (\控制码1 ), .\选择码2 (\控制码2 ), .\选择码3 (\控制码3 ), .\选择码4 (\控制码4 ),
    .out_21(out_133));
  \_16选1选择器  \u_16选1选择器_2  (
    ._0000(in_2), ._0001(in_10), ._0010(in_18), ._0011(in_26), ._0100(in_34), ._0101(in_42), ._0110(in_50),
    ._0111(in_58), ._1000(in_66), ._1001(in_74), ._1010(in_82), ._1011(in_90), ._1100(in_98), ._1101(in_106),
    ._1110(in_114), ._1111(in_122), .\选择码1 (\控制码1 ), .\选择码2 (\控制码2 ), .\选择码3 (\控制码3 ), .\选择码4 (\控制码4 ),
    .out_21(out_134));
  \_16选1选择器  \u_16选1选择器_3  (
    ._0000(in_3), ._0001(in_11), ._0010(in_19), ._0011(in_27), ._0100(in_35), ._0101(in_43), ._0110(in_51),
    ._0111(in_59), ._1000(in_67), ._1001(in_75), ._1010(in_83), ._1011(in_91), ._1100(in_99), ._1101(in_107),
    ._1110(in_115), ._1111(in_123), .\选择码1 (\控制码1 ), .\选择码2 (\控制码2 ), .\选择码3 (\控制码3 ), .\选择码4 (\控制码4 ),
    .out_21(out_135));
  \_16选1选择器  \u_16选1选择器_4  (
    ._0000(in_4), ._0001(in_12), ._0010(in_20), ._0011(in_28), ._0100(in_36), ._0101(in_44), ._0110(in_52),
    ._0111(in_60), ._1000(in_68), ._1001(in_76), ._1010(in_84), ._1011(in_92), ._1100(in_100),
    ._1101(in_108), ._1110(in_116), ._1111(in_124), .\选择码1 (\控制码1 ), .\选择码2 (\控制码2 ), .\选择码3 (\控制码3 ),
    .\选择码4 (\控制码4 ), .out_21(out_136));
  \_16选1选择器  \u_16选1选择器_5  (
    ._0000(in_5), ._0001(in_13), ._0010(in_21), ._0011(in_29), ._0100(in_37), ._0101(in_45), ._0110(in_53),
    ._0111(in_61), ._1000(in_69), ._1001(in_77), ._1010(in_85), ._1011(in_93), ._1100(in_101),
    ._1101(in_109), ._1110(in_117), ._1111(in_125), .\选择码1 (\控制码1 ), .\选择码2 (\控制码2 ), .\选择码3 (\控制码3 ),
    .\选择码4 (\控制码4 ), .out_21(out_137));
  \_16选1选择器  \u_16选1选择器_6  (
    ._0000(in_6), ._0001(in_14), ._0010(in_22), ._0011(in_30), ._0100(in_38), ._0101(in_46), ._0110(in_54),
    ._0111(in_62), ._1000(in_70), ._1001(in_78), ._1010(in_86), ._1011(in_94), ._1100(in_102),
    ._1101(in_110), ._1110(in_118), ._1111(in_126), .\选择码1 (\控制码1 ), .\选择码2 (\控制码2 ), .\选择码3 (\控制码3 ),
    .\选择码4 (\控制码4 ), .out_21(out_138));
  \_16选1选择器  \u_16选1选择器_7  (
    ._0000(in_7), ._0001(in_15), ._0010(in_23), ._0011(in_31), ._0100(in_39), ._0101(in_47), ._0110(in_55),
    ._0111(in_63), ._1000(in_71), ._1001(in_79), ._1010(in_87), ._1011(in_95), ._1100(in_103),
    ._1101(in_111), ._1110(in_119), ._1111(in_127), .\选择码1 (\控制码1 ), .\选择码2 (\控制码2 ), .\选择码3 (\控制码3 ),
    .\选择码4 (\控制码4 ), .out_21(out_139));
  \_16选1选择器  \u_16选1选择器_8  (
    ._0000(in_8), ._0001(in_16), ._0010(in_24), ._0011(in_32), ._0100(in_40), ._0101(in_48), ._0110(in_56),
    ._0111(in_64), ._1000(in_72), ._1001(in_80), ._1010(in_88), ._1011(in_96), ._1100(in_104),
    ._1101(in_112), ._1110(in_120), ._1111(in_128), .\选择码1 (\控制码1 ), .\选择码2 (\控制码2 ), .\选择码3 (\控制码3 ),
    .\选择码4 (\控制码4 ), .out_21(out_140));
endmodule
