// Logisim project 8位带宽的2选1选择器.circ as structural Verilog: 1 circuit, main circuit 8位2选1选择器
module \_8位2选1选择器  (
  input  \输入1第1位 ,
  input  \输入1第2位 ,
  input  \输入1第3位 ,
  input  \输入1第4位 ,
  input  \输入1第5位 ,
  input  \输入1第6位 ,
  input  \输入1第7位 ,
  input  \输入1第8位 ,
  input  \输入2第1位 ,
  input  \输入2第2位 ,
  input  \输入2第3位 ,
  input  \输入2第4位 ,
  input  \输入2第5位 ,
  input  \输入2第6位 ,
  input  \输入2第7位 ,
  input  \输入2第8位 ,
  input  \操控码 ,
  output out_18,
  output out_19,
  output out_20,
  output out_21,
  output out_22,
  output out_23,
  output out_24,
  output out_25
);

  \_2选1选择器  \u_2选1选择器_1  (.\输入1 (\输入1第1位 ), .\输入2 (\输入2第1位 ), .\选择_1表示输入1_0表示输入2 (\操控码 ), .\输出 (out_18));
  \_2选1选择器  \u_2选1选择器_2  (.\输入1 (\输入1第2位 ), .\输入2 (\输入2第2位 ), .\选择_1表示输入1_0表示输入2 (\操控码 ), .\输出 (out_19));
  \_2选1选择器  \u_2选1选择器_3  (.\输入1 (\输入1第3位 ), .\输入2 (\输入2第3位 ), .\选择_1表示输入1_0表示输入2 (\操控码 ), .\输出 (out_20));
  \_2选1选择器  \u_2选1选择器_4  (.\输入1 (\输入1第4位 ), .\输入2 (\输入2第4位 ), .\选择_1表示输入1_0表示输入2 (\操控码 ), .\输出 (out_21));
  \_2选1选择器  \u_2选1选择器_5  (.\输入1 (\输入1第5位 ), .\输入2 (\输入2第5位 ), .\选择_1表示输入1_0表示输入2 (\操控码 ), .\输出 (out_22));
  \_2选1选择器  \u_2选1选择器_6  (.\输入1 (\输入1第6位 ), .\输入2 (\输入2第6位 ), .\选择_1表示输入1_0表示输入2 (\操控码 ), .\输出 (out_23));
  \_2选1选择器  \u_2选1选择器_7  (.\输入1 (\输入1第7位 ), .\输入2 (\输入2第7位 ), .\选择_1表示输入1_0表示输入2 (\操控码 ), .\输出 (out_24));
  \_2选1选择器  \u_2选1选择器_8  (.\输入1 (\输入1第8位 ), .\输入2 (\输入2第8位 ), .\选择_1表示输入1_0表示输入2 (\操控码 ), .\输出 (out_25));
endmodule
