// Logisim project 未完成的8位带宽的256选1选择器.circ as structural Verilog: 1 circuit, main circuit main
module main (
  input  [7:0] in_1,
  input  [7:0] in_2,
  input  [7:0] in_3,
  input  [7:0] in_4,
  input  [7:0] in_5,
  input  [7:0] in_6,
  input  [7:0] in_7,
  input  [7:0] in_8,
  input  [7:0] in_9,
  input  [7:0] in_10,
  input  [7:0] in_11,
  input  [7:0] in_12,
  input  [7:0] in_13,
  input  [7:0] in_14,
  input  [7:0] in_15,
  input  [7:0] in_16,
  input  [7:0] in_17,
  input  [7:0] in_18,
  input  [7:0] in_19,
  input  [7:0] in_20,
  input  [7:0] in_21,
  input  [7:0] in_22,
  input  [7:0] in_23,
  input  [7:0] in_24,
  input  [7:0] in_25,
  input  [7:0] in_26,
  input  [7:0] in_27,
  input  [7:0] in_28,
  input  [7:0] in_29,
  input  [7:0] in_30,
  input  [7:0] in_31,
  input  [7:0] in_32,
  input  [7:0] in_33,
  input  [7:0] in_34,
  input  [7:0] in_35,
  input  [7:0] in_36,
  input  [7:0] in_37,
  input  [7:0] in_38,
  input  [7:0] in_39,
  input  [7:0] in_40,
  input  [7:0] in_41,
  input  [7:0] in_42,
  input  [7:0] in_43,
  input  [7:0] in_44,
  input  [7:0] in_45,
  input  [7:0] in_46,
  input  [7:0] in_47,
  input  [7:0] in_48,
  input  [7:0] in_49,
  input  [7:0] in_50,
  input  [7:0] in_51,
  input  [7:0] in_52,
  input  [7:0] in_53,
  input  [7:0] in_54,
  input  [7:0] in_55,
  input  [7:0] in_56,
  input  [7:0] in_57,
  input  [7:0] in_58,
  input  [7:0] in_59,
  input  [7:0] in_60,
  input  [7:0] in_61,
  input  [7:0] in_62,
  input  [7:0] in_63,
  input  [7:0] in_64,
  input  [7:0] in_65,
  input  [7:0] in_66,
  input  [7:0] in_67,
  input  [7:0] in_68,
  input  [7:0] in_69,
  input  [7:0] in_70,
  input  [7:0] in_71,
  input  [7:0] in_72,
  input  [7:0] in_73,
  input  [7:0] in_74,
  input  [7:0] in_75,
  input  [7:0] in_76,
  input  [7:0] in_77,
  input  [7:0] in_78,
  input  [7:0] in_79,
  input  [7:0] in_80,
  input  [7:0] in_81,
  input  [7:0] in_82,
  input  [7:0] in_83,
  input  [7:0] in_84,
  input  [7:0] in_85,
  input  [7:0] in_86,
  input  [7:0] in_87,
  input  [7:0] in_88,
  input  [7:0] in_89,
  input  [7:0] in_90,
  input  [7:0] in_91,
  input  [7:0] in_92,
  input  [7:0] in_93,
  input  [7:0] in_94,
  input  [7:0] in_95,
  input  [7:0] in_96,
  input  [7:0] in_97,
  input  [7:0] in_98,
  input  [7:0] in_99,
  input  [7:0] in_100,
  input  [7:0] in_101,
  input  [7:0] in_102,
  input  [7:0] in_103,
  input  [7:0] in_104,
  input  [7:0] in_105,
  input  [7:0] in_106,
  input  [7:0] in_107,
  input  [7:0] in_108,
  input  [7:0] in_109,
  input  [7:0] in_110,
  input  [7:0] in_111,
  input  [7:0] in_112,
  input  [7:0] in_113,
  input  [7:0] in_114,
  input  [7:0] in_115,
  input  [7:0] in_116,
  input  [7:0] in_117,
  input  [7:0] in_118,
  input  [7:0] in_119,
  input  [7:0] in_120,
  input  [7:0] in_121,
  input  [7:0] in_122,
  input  [7:0] in_123,
  input  [7:0] in_124,
  input  [7:0] in_125,
  input  [7:0] in_126,
  input  [7:0] in_127,
  input  [7:0] in_128,
  input  [7:0] in_129,
  input  [7:0] in_130,
  input  [7:0] in_131,
  input  [7:0] in_132,
  input  [7:0] in_133,
  input  [7:0] in_134,
  input  [7:0] in_135,
  input  [7:0] in_136,
  input  [7:0] in_137,
  input  [7:0] in_138,
  input  [7:0] in_139,
  input  [7:0] in_140,
  input  [7:0] in_141,
  input  [7:0] in_142,
  input  [7:0] in_143,
  input  [7:0] in_144,
  input  [7:0] in_145,
  input  [7:0] in_146,
  input  [7:0] in_147,
  input  [7:0] in_148,
  input  [7:0] in_149,
  input  [7:0] in_150,
  input  [7:0] in_151,
  input  [7:0] in_152,
  input  [7:0] in_153,
  input  [7:0] in_154,
  input  [7:0] in_155,
  input  [7:0] in_156,
  input  [7:0] in_157,
  input  [7:0] in_158,
  input  [7:0] in_159,
  input  [7:0] in_160,
  input  [7:0] in_161,
  input  [7:0] in_162,
  input  [7:0] in_163,
  input  [7:0] in_164,
  input  [7:0] in_165,
  input  [7:0] in_166,
  input  [7:0] in_167,
  input  [7:0] in_168,
  input  [7:0] in_169,
  input  [7:0] in_170,
  input  [7:0] in_171,
  input  [7:0] in_172,
  input  [7:0] in_173,
  input  [7:0] in_174,
  input  [7:0] in_175,
  input  [7:0] in_176,
  input  [7:0] in_177,
  input  [7:0] in_178,
  input  [7:0] in_179,
  input  [7:0] in_180,
  input  [7:0] in_181,
  input  [7:0] in_182,
  input  [7:0] in_183,
  input  [7:0] in_184,
  input  [7:0] in_185,
  input  [7:0] in_186,
  input  [7:0] in_187,
  input  [7:0] in_188,
  input  [7:0] in_189,
  input  [7:0] in_190,
  input  [7:0] in_191,
  input  [7:0] in_192,
  input  [7:0] in_193,
  input  [7:0] in_194,
  input  [7:0] in_195,
  input  [7:0] in_196,
  input  [7:0] in_197,
  input  [7:0] in_198,
  input  [7:0] in_199,
  input  [7:0] in_200,
  input  [7:0] in_201,
  input  [7:0] in_202,
  input  [7:0] in_203,
  input  [7:0] in_204,
  input  [7:0] in_205,
  input  [7:0] in_206,
  input  [7:0] in_207,
  input  [7:0] in_208,
  input  [7:0] in_209,
  input  [7:0] in_210,
  input  [7:0] in_211,
  input  [7:0] in_212,
  input  [7:0] in_213,
  input  [7:0] in_214,
  input  [7:0] in_215,
  input  [7:0] in_216,
  input  [7:0] in_217,
  input  [7:0] in_218,
  input  [7:0] in_219,
  input  [7:0] in_220,
  input  [7:0] in_221,
  input  [7:0] in_222,
  input  [7:0] in_223,
  input  [7:0] in_224,
  input  [7:0] in_225,
  input  [7:0] in_226,
  input  [7:0] in_227,
  input  [7:0] in_228,
  input  [7:0] in_229,
  input  [7:0] in_230,
  input  [7:0] in_231,
  input  [7:0] in_232,
  input  [7:0] in_233,
  input  [7:0] in_234,
  input  [7:0] in_235,
  input  [7:0] in_236,
  input  [7:0] in_237,
  input  [7:0] in_238,
  input  [7:0] in_239,
  input  [7:0] in_240,
  input  [7:0] in_241,
  input  [7:0] in_242,
  input  [7:0] in_243,
  input  [7:0] in_244,
  input  [7:0] in_245,
  input  [7:0] in_246,
  input  [7:0] in_247,
  input  [7:0] in_248,
  input  [7:0] in_249,
  input  [7:0] in_250,
  input  [7:0] in_251,
  input  [7:0] in_252,
  input  [7:0] in_253,
  input  [7:0] in_254,
  input  [7:0] in_255,
  input  [7:0] in_256,
  input  [7:0] \控制码 ,
  output [7:0] out_258
);

  wire [7:0] \n8位接口带宽的16选1选择器_1_out_21 , \n8位接口带宽的16选1选择器_2_out_21 , \n8位接口带宽的16选1选择器_3_out_21 ,
       \n8位接口带宽的16选1选择器_4_out_21 , \n8位接口带宽的16选1选择器_5_out_21 , \n8位接口带宽的16选1选择器_6_out_21 ,
       \n8位接口带宽的16选1选择器_7_out_21 , \n8位接口带宽的16选1选择器_8_out_21 , \n8位接口带宽的16选1选择器_9_out_21 ,
       \n8位接口带宽的16选1选择器_10_out_21 , \n8位接口带宽的16选1选择器_11_out_21 , \n8位接口带宽的16选1选择器_12_out_21 ,
       \n8位接口带宽的16选1选择器_13_out_21 , \n8位接口带宽的16选1选择器_14_out_21 , \n8位接口带宽的16选1选择器_15_out_21 ,
       \n8位接口带宽的16选1选择器_16_out_21 ;

  \_8位接口带宽的16选1选择器  \u_8位接口带宽的16选1选择器_1  (
    .\第一个8位输入 (in_1), .\第二个8位输入 (in_2), .\第三个8位输入 (in_3), .\第四个8位输入 (in_4), .\第五个8位输入 (in_5),
    .\第六个8位输入 (in_6), .\第七个8位输入 (in_7), .\第八个8位输入 (in_8), .\第九个8位输入 (in_9), .\第十个8位输入 (in_10),
    .\第11个8位输入 (in_11), .\第12个8位输入 (in_12), .\第13个8位输入 (in_13), .\第14个8位输入 (in_14), .\第15个8位输入 (in_15),
    .\第16个8位输入 (in_16), .\控制码1 (\控制码 [0]), .\控制码2 (\控制码 [1]), .\控制码3 (\控制码 [2]), .\控制码4 (\控制码 [3]),
    .out_21(\n8位接口带宽的16选1选择器_1_out_21 ));
  \_8位接口带宽的16选1选择器  \u_8位接口带宽的16选1选择器_2  (
    .\第一个8位输入 (in_17), .\第二个8位输入 (in_18), .\第三个8位输入 (in_19), .\第四个8位输入 (in_20), .\第五个8位输入 (in_21),
    .\第六个8位输入 (in_22), .\第七个8位输入 (in_23), .\第八个8位输入 (in_24), .\第九个8位输入 (in_25), .\第十个8位输入 (in_26),
    .\第11个8位输入 (in_27), .\第12个8位输入 (in_28), .\第13个8位输入 (in_29), .\第14个8位输入 (in_30), .\第15个8位输入 (in_31),
    .\第16个8位输入 (in_32), .\控制码1 (\控制码 [0]), .\控制码2 (\控制码 [1]), .\控制码3 (\控制码 [2]), .\控制码4 (\控制码 [3]),
    .out_21(\n8位接口带宽的16选1选择器_2_out_21 ));
  \_8位接口带宽的16选1选择器  \u_8位接口带宽的16选1选择器_3  (
    .\第一个8位输入 (in_33), .\第二个8位输入 (in_34), .\第三个8位输入 (in_35), .\第四个8位输入 (in_36), .\第五个8位输入 (in_37),
    .\第六个8位输入 (in_38), .\第七个8位输入 (in_39), .\第八个8位输入 (in_40), .\第九个8位输入 (in_41), .\第十个8位输入 (in_42),
    .\第11个8位输入 (in_43), .\第12个8位输入 (in_44), .\第13个8位输入 (in_45), .\第14个8位输入 (in_46), .\第15个8位输入 (in_47),
    .\第16个8位输入 (in_48), .\控制码1 (\控制码 [0]), .\控制码2 (\控制码 [1]), .\控制码3 (\控制码 [2]), .\控制码4 (\控制码 [3]),
    .out_21(\n8位接口带宽的16选1选择器_3_out_21 ));
  \_8位接口带宽的16选1选择器  \u_8位接口带宽的16选1选择器_4  (
    .\第一个8位输入 (in_49), .\第二个8位输入 (in_50), .\第三个8位输入 (in_51), .\第四个8位输入 (in_52), .\第五个8位输入 (in_53),
    .\第六个8位输入 (in_54), .\第七个8位输入 (in_55), .\第八个8位输入 (in_56), .\第九个8位输入 (in_57), .\第十个8位输入 (in_58),
    .\第11个8位输入 (in_59), .\第12个8位输入 (in_60), .\第13个8位输入 (in_61), .\第14个8位输入 (in_62), .\第15个8位输入 (in_63),
    .\第16个8位输入 (in_64), .\控制码1 (\控制码 [0]), .\控制码2 (\控制码 [1]), .\控制码3 (\控制码 [2]), .\控制码4 (\控制码 [3]),
    .out_21(\n8位接口带宽的16选1选择器_4_out_21 ));
  \_8位接口带宽的16选1选择器  \u_8位接口带宽的16选1选择器_5  (
    .\第一个8位输入 (in_65), .\第二个8位输入 (in_66), .\第三个8位输入 (in_67), .\第四个8位输入 (in_68), .\第五个8位输入 (in_69),
    .\第六个8位输入 (in_70), .\第七个8位输入 (in_71), .\第八个8位输入 (in_72), .\第九个8位输入 (in_73), .\第十个8位输入 (in_74),
    .\第11个8位输入 (in_75), .\第12个8位输入 (in_76), .\第13个8位输入 (in_77), .\第14个8位输入 (in_78), .\第15个8位输入 (in_79),
    .\第16个8位输入 (in_80), .\控制码1 (\控制码 [0]), .\控制码2 (\控制码 [1]), .\控制码3 (\控制码 [2]), .\控制码4 (\控制码 [3]),
    .out_21(\n8位接口带宽的16选1选择器_5_out_21 ));
  \_8位接口带宽的16选1选择器  \u_8位接口带宽的16选1选择器_6  (
    .\第一个8位输入 (in_81), .\第二个8位输入 (in_82), .\第三个8位输入 (in_83), .\第四个8位输入 (in_84), .\第五个8位输入 (in_85),
    .\第六个8位输入 (in_86), .\第七个8位输入 (in_87), .\第八个8位输入 (in_88), .\第九个8位输入 (in_89), .\第十个8位输入 (in_90),
    .\第11个8位输入 (in_91), .\第12个8位输入 (in_92), .\第13个8位输入 (in_93), .\第14个8位输入 (in_94), .\第15个8位输入 (in_95),
    .\第16个8位输入 (in_96), .\控制码1 (\控制码 [0]), .\控制码2 (\控制码 [1]), .\控制码3 (\控制码 [2]), .\控制码4 (\控制码 [3]),
    .out_21(\n8位接口带宽的16选1选择器_6_out_21 ));
  \_8位接口带宽的16选1选择器  \u_8位接口带宽的16选1选择器_7  (
    .\第一个8位输入 (in_97), .\第二个8位输入 (in_98), .\第三个8位输入 (in_99), .\第四个8位输入 (in_100), .\第五个8位输入 (in_101),
    .\第六个8位输入 (in_102), .\第七个8位输入 (in_103), .\第八个8位输入 (in_104), .\第九个8位输入 (in_105), .\第十个8位输入 (in_106),
    .\第11个8位输入 (in_107), .\第12个8位输入 (in_108), .\第13个8位输入 (in_109), .\第14个8位输入 (in_110), .\第15个8位输入 (in_111),
    .\第16个8位输入 (in_112), .\控制码1 (\控制码 [0]), .\控制码2 (\控制码 [1]), .\控制码3 (\控制码 [2]), .\控制码4 (\控制码 [3]),
    .out_21(\n8位接口带宽的16选1选择器_7_out_21 ));
  \_8位接口带宽的16选1选择器  \u_8位接口带宽的16选1选择器_8  (
    .\第一个8位输入 (in_113), .\第二个8位输入 (in_114), .\第三个8位输入 (in_115), .\第四个8位输入 (in_116), .\第五个8位输入 (in_117),
    .\第六个8位输入 (in_118), .\第七个8位输入 (in_119), .\第八个8位输入 (in_120), .\第九个8位输入 (in_121), .\第十个8位输入 (in_122),
    .\第11个8位输入 (in_123), .\第12个8位输入 (in_124), .\第13个8位输入 (in_125), .\第14个8位输入 (in_126), .\第15个8位输入 (in_127),
    .\第16个8位输入 (in_128), .\控制码1 (\控制码 [0]), .\控制码2 (\控制码 [1]), .\控制码3 (\控制码 [2]), .\控制码4 (\控制码 [3]),
    .out_21(\n8位接口带宽的16选1选择器_8_out_21 ));
  \_8位接口带宽的16选1选择器  \u_8位接口带宽的16选1选择器_9  (
    .\第一个8位输入 (in_129), .\第二个8位输入 (in_130), .\第三个8位输入 (in_131), .\第四个8位输入 (in_132), .\第五个8位输入 (in_133),
    .\第六个8位输入 (in_134), .\第七个8位输入 (in_135), .\第八个8位输入 (in_136), .\第九个8位输入 (in_137), .\第十个8位输入 (in_138),
    .\第11个8位输入 (in_139), .\第12个8位输入 (in_140), .\第13个8位输入 (in_141), .\第14个8位输入 (in_142), .\第15个8位输入 (in_143),
    .\第16个8位输入 (in_144), .\控制码1 (\控制码 [0]), .\控制码2 (\控制码 [1]), .\控制码3 (\控制码 [2]), .\控制码4 (\控制码 [3]),
    .out_21(\n8位接口带宽的16选1选择器_9_out_21 ));
  \_8位接口带宽的16选1选择器  \u_8位接口带宽的16选1选择器_10  (
    .\第一个8位输入 (in_145), .\第二个8位输入 (in_146), .\第三个8位输入 (in_147), .\第四个8位输入 (in_148), .\第五个8位输入 (in_149),
    .\第六个8位输入 (in_150), .\第七个8位输入 (in_151), .\第八个8位输入 (in_152), .\第九个8位输入 (in_153), .\第十个8位输入 (in_154),
    .\第11个8位输入 (in_155), .\第12个8位输入 (in_156), .\第13个8位输入 (in_157), .\第14个8位输入 (in_158), .\第15个8位输入 (in_159),
    .\第16个8位输入 (in_160), .\控制码1 (\控制码 [0]), .\控制码2 (\控制码 [1]), .\控制码3 (\控制码 [2]), .\控制码4 (\控制码 [3]),
    .out_21(\n8位接口带宽的16选1选择器_10_out_21 ));
  \_8位接口带宽的16选1选择器  \u_8位接口带宽的16选1选择器_11  (
    .\第一个8位输入 (in_161), .\第二个8位输入 (in_162), .\第三个8位输入 (in_163), .\第四个8位输入 (in_164), .\第五个8位输入 (in_165),
    .\第六个8位输入 (in_166), .\第七个8位输入 (in_167), .\第八个8位输入 (in_168), .\第九个8位输入 (in_169), .\第十个8位输入 (in_170),
    .\第11个8位输入 (in_171), .\第12个8位输入 (in_172), .\第13个8位输入 (in_173), .\第14个8位输入 (in_174), .\第15个8位输入 (in_175),
    .\第16个8位输入 (in_176), .\控制码1 (\控制码 [0]), .\控制码2 (\控制码 [1]), .\控制码3 (\控制码 [2]), .\控制码4 (\控制码 [3]),
    .out_21(\n8位接口带宽的16选1选择器_11_out_21 ));
  \_8位接口带宽的16选1选择器  \u_8位接口带宽的16选1选择器_12  (
    .\第一个8位输入 (in_177), .\第二个8位输入 (in_178), .\第三个8位输入 (in_179), .\第四个8位输入 (in_180), .\第五个8位输入 (in_181),
    .\第六个8位输入 (in_182), .\第七个8位输入 (in_183), .\第八个8位输入 (in_184), .\第九个8位输入 (in_185), .\第十个8位输入 (in_186),
    .\第11个8位输入 (in_187), .\第12个8位输入 (in_188), .\第13个8位输入 (in_189), .\第14个8位输入 (in_190), .\第15个8位输入 (in_191),
    .\第16个8位输入 (in_192), .\控制码1 (\控制码 [0]), .\控制码2 (\控制码 [1]), .\控制码3 (\控制码 [2]), .\控制码4 (\控制码 [3]),
    .out_21(\n8位接口带宽的16选1选择器_12_out_21 ));
  \_8位接口带宽的16选1选择器  \u_8位接口带宽的16选1选择器_13  (
    .\第一个8位输入 (in_193), .\第二个8位输入 (in_194), .\第三个8位输入 (in_195), .\第四个8位输入 (in_196), .\第五个8位输入 (in_197),
    .\第六个8位输入 (in_198), .\第七个8位输入 (in_199), .\第八个8位输入 (in_200), .\第九个8位输入 (in_201), .\第十个8位输入 (in_202),
    .\第11个8位输入 (in_203), .\第12个8位输入 (in_204), .\第13个8位输入 (in_205), .\第14个8位输入 (in_206), .\第15个8位输入 (in_207),
    .\第16个8位输入 (in_208), .\控制码1 (\控制码 [0]), .\控制码2 (\控制码 [1]), .\控制码3 (\控制码 [2]), .\控制码4 (\控制码 [3]),
    .out_21(\n8位接口带宽的16选1选择器_13_out_21 ));
  \_8位接口带宽的16选1选择器  \u_8位接口带宽的16选1选择器_14  (
    .\第一个8位输入 (in_209), .\第二个8位输入 (in_210), .\第三个8位输入 (in_211), .\第四个8位输入 (in_212), .\第五个8位输入 (in_213),
    .\第六个8位输入 (in_214), .\第七个8位输入 (in_215), .\第八个8位输入 (in_216), .\第九个8位输入 (in_217), .\第十个8位输入 (in_218),
    .\第11个8位输入 (in_219), .\第12个8位输入 (in_220), .\第13个8位输入 (in_221), .\第14个8位输入 (in_222), .\第15个8位输入 (in_223),
    .\第16个8位输入 (in_224), .\控制码1 (\控制码 [0]), .\控制码2 (\控制码 [1]), .\控制码3 (\控制码 [2]), .\控制码4 (\控制码 [3]),
    .out_21(\n8位接口带宽的16选1选择器_14_out_21 ));
  \_8位接口带宽的16选1选择器  \u_8位接口带宽的16选1选择器_15  (
    .\第一个8位输入 (in_225), .\第二个8位输入 (in_226), .\第三个8位输入 (in_227), .\第四个8位输入 (in_228), .\第五个8位输入 (in_229),
    .\第六个8位输入 (in_230), .\第七个8位输入 (in_231), .\第八个8位输入 (in_232), .\第九个8位输入 (in_233), .\第十个8位输入 (in_234),
    .\第11个8位输入 (in_235), .\第12个8位输入 (in_236), .\第13个8位输入 (in_237), .\第14个8位输入 (in_238), .\第15个8位输入 (in_239),
    .\第16个8位输入 (in_240), .\控制码1 (\控制码 [0]), .\控制码2 (\控制码 [1]), .\控制码3 (\控制码 [2]), .\控制码4 (\控制码 [3]),
    .out_21(\n8位接口带宽的16选1选择器_15_out_21 ));
  \_8位接口带宽的16选1选择器  \u_8位接口带宽的16选1选择器_16  (
    .\第一个8位输入 (in_241), .\第二个8位输入 (in_242), .\第三个8位输入 (in_243), .\第四个8位输入 (in_244), .\第五个8位输入 (in_245),
    .\第六个8位输入 (in_246), .\第七个8位输入 (in_247), .\第八个8位输入 (in_248), .\第九个8位输入 (in_249), .\第十个8位输入 (in_250),
    .\第11个8位输入 (in_251), .\第12个8位输入 (in_252), .\第13个8位输入 (in_253), .\第14个8位输入 (in_254), .\第15个8位输入 (in_255),
    .\第16个8位输入 (in_256), .\控制码1 (\控制码 [0]), .\控制码2 (\控制码 [1]), .\控制码3 (\控制码 [2]), .\控制码4 (\控制码 [3]),
    .out_21(\n8位接口带宽的16选1选择器_16_out_21 ));
  \_8位接口带宽的16选1选择器  \u_8位接口带宽的16选1选择器_17  (
    .\第一个8位输入 (\n8位接口带宽的16选1选择器_1_out_21 ), .\第二个8位输入 (\n8位接口带宽的16选1选择器_2_out_21 ),
    .\第三个8位输入 (\n8位接口带宽的16选1选择器_3_out_21 ), .\第四个8位输入 (\n8位接口带宽的16选1选择器_4_out_21 ),
    .\第五个8位输入 (\n8位接口带宽的16选1选择器_5_out_21 ), .\第六个8位输入 (\n8位接口带宽的16选1选择器_6_out_21 ),
    .\第七个8位输入 (\n8位接口带宽的16选1选择器_7_out_21 ), .\第八个8位输入 (\n8位接口带宽的16选1选择器_8_out_21 ),
    .\第九个8位输入 (\n8位接口带宽的16选1选择器_9_out_21 ), .\第十个8位输入 (\n8位接口带宽的16选1选择器_10_out_21 ),
    .\第11个8位输入 (\n8位接口带宽的16选1选择器_11_out_21 ), .\第12个8位输入 (\n8位接口带宽的16选1选择器_12_out_21 ),
    .\第13个8位输入 (\n8位接口带宽的16选1选择器_13_out_21 ), .\第14个8位输入 (\n8位接口带宽的16选1选择器_14_out_21 ),
    .\第15个8位输入 (\n8位接口带宽的16选1选择器_15_out_21 ), .\第16个8位输入 (\n8位接口带宽的16选1选择器_16_out_21 ), .\控制码1 (\控制码 [4]),
    .\控制码2 (\控制码 [5]), .\控制码3 (\控制码 [6]), .\控制码4 (\控制码 [7]), .out_21(out_258));
endmodule
