// Logisim project 4位输入OP.circ as structural Verilog: 1 circuit, main circuit 4位输入op
module \_4位输入op  (
  input  \输入第1位 ,
  input  \输入第2位 ,
  input  \输入第3位 ,
  input  \输入第4位 ,
  output \输入_0000 ,
  output \输入_0001 ,
  output \输入_0010 ,
  output \输入_0011 ,
  output \输入_0100 ,
  output \输入_0101 ,
  output \输入_0110 ,
  output \输入_0111 ,
  output \输入_1000 ,
  output \输入_1001 ,
  output \输入_1010 ,
  output \输入_1011 ,
  output \输入_1100 ,
  output \输入_1101 ,
  output \输入_1110 ,
  output \输入_1111 
);

  wire inverter_1_output, inverter_2_output, inverter_3_output, inverter_4_output;

  Inverter inverter_1 (.Input(\输入第1位 ), .Output(inverter_1_output));
  Inverter inverter_2 (.Input(\输入第2位 ), .Output(inverter_2_output));
  Inverter inverter_3 (.Input(\输入第3位 ), .Output(inverter_3_output));
  Inverter inverter_4 (.Input(\输入第4位 ), .Output(inverter_4_output));
  \_4位与门  \u_4位与门_1  (
    .\第一位输入 (inverter_1_output), .\第二位输入 (inverter_2_output), .\第三位输入 (inverter_3_output),
    .\第四位输入 (inverter_4_output), .\输出 (\输入_0000 ));
  \_4位与门  \u_4位与门_2  (
    .\第一位输入 (inverter_1_output), .\第二位输入 (inverter_2_output), .\第三位输入 (\输入第3位 ), .\第四位输入 (inverter_4_output),
    .\输出 (\输入_0010 ));
  \_4位与门  \u_4位与门_3  (
    .\第一位输入 (inverter_1_output), .\第二位输入 (\输入第2位 ), .\第三位输入 (inverter_3_output), .\第四位输入 (inverter_4_output),
    .\输出 (\输入_0100 ));
  \_4位与门  \u_4位与门_4  (
    .\第一位输入 (inverter_1_output), .\第二位输入 (\输入第2位 ), .\第三位输入 (inverter_3_output), .\第四位输入 (\输入第4位 ),
    .\输出 (\输入_0101 ));
  \_4位与门  \u_4位与门_5  (
    .\第一位输入 (\输入第1位 ), .\第二位输入 (inverter_2_output), .\第三位输入 (inverter_3_output), .\第四位输入 (inverter_4_output),
    .\输出 (\输入_1000 ));
  \_4位与门  \u_4位与门_6  (
    .\第一位输入 (\输入第1位 ), .\第二位输入 (inverter_2_output), .\第三位输入 (\输入第3位 ), .\第四位输入 (inverter_4_output),
    .\输出 (\输入_1010 ));
  \_4位与门  \u_4位与门_7  (
    .\第一位输入 (\输入第1位 ), .\第二位输入 (\输入第2位 ), .\第三位输入 (inverter_3_output), .\第四位输入 (inverter_4_output),
    .\输出 (\输入_1100 ));
  \_4位与门  \u_4位与门_8  (
    .\第一位输入 (\输入第1位 ), .\第二位输入 (\输入第2位 ), .\第三位输入 (\输入第3位 ), .\第四位输入 (inverter_4_output), .\输出 (\输入_1110 ));
  \_4位与门  \u_4位与门_9  (
    .\第一位输入 (inverter_1_output), .\第二位输入 (inverter_2_output), .\第三位输入 (inverter_3_output), .\第四位输入 (\输入第4位 ),
    .\输出 (\输入_0001 ));
  \_4位与门  \u_4位与门_10  (
    .\第一位输入 (inverter_1_output), .\第二位输入 (inverter_2_output), .\第三位输入 (\输入第3位 ), .\第四位输入 (\输入第4位 ),
    .\输出 (\输入_0011 ));
  \_4位与门  \u_4位与门_11  (
    .\第一位输入 (inverter_1_output), .\第二位输入 (\输入第2位 ), .\第三位输入 (\输入第3位 ), .\第四位输入 (inverter_4_output),
    .\输出 (\输入_0110 ));
  \_4位与门  \u_4位与门_12  (
    .\第一位输入 (inverter_1_output), .\第二位输入 (\输入第2位 ), .\第三位输入 (\输入第3位 ), .\第四位输入 (\输入第4位 ), .\输出 (\输入_0111 ));
  \_4位与门  \u_4位与门_13  (
    .\第一位输入 (\输入第1位 ), .\第二位输入 (inverter_2_output), .\第三位输入 (inverter_3_output), .\第四位输入 (\输入第4位 ),
    .\输出 (\输入_1001 ));
  \_4位与门  \u_4位与门_14  (
    .\第一位输入 (\输入第1位 ), .\第二位输入 (inverter_2_output), .\第三位输入 (\输入第3位 ), .\第四位输入 (\输入第4位 ), .\输出 (\输入_1011 ));
  \_4位与门  \u_4位与门_15  (
    .\第一位输入 (\输入第1位 ), .\第二位输入 (\输入第2位 ), .\第三位输入 (inverter_3_output), .\第四位输入 (\输入第4位 ), .\输出 (\输入_1101 ));
  \_4位与门  \u_4位与门_16  (.\第一位输入 (\输入第1位 ), .\第二位输入 (\输入第2位 ), .\第三位输入 (\输入第3位 ), .\第四位输入 (\输入第4位 ), .\输出 (\输入_1111 ));
endmodule
