// Logisim project CPU.circ as structural Verilog: 1 circuit, main circuit CPU
module CPU (
  input  \时钟信号 ,
  input  \写使能信号 ,
  input  \RST信号 ,
  output out_4,
  output out_5,
  output out_6,
  output out_7,
  output out_8,
  output out_9,
  output out_10,
  output out_11
);

  wire alu_1_out_21, alu_1_out_22, alu_1_out_23, alu_1_out_24, alu_1_out_25, alu_1_out_26, alu_1_out_27,
       alu_1_out_28, \n8位单刀双掷开关_1_out_10 , \n8位单刀双掷开关_1_out_11 , \n8位单刀双掷开关_1_out_12 , \n8位单刀双掷开关_1_out_13 ,
       \n8位单刀双掷开关_1_out_14 , \n8位单刀双掷开关_1_out_15 , \n8位单刀双掷开关_1_out_16 , \n8位单刀双掷开关_1_out_17 ,
       pc_rom_ir_1_out_16, pc_rom_ir_1_out_17, pc_rom_ir_1_out_18, pc_rom_ir_1_out_19;
  wire [3:0] pc_rom_ir_1_out_12;
  wire [7:4] \n2to1单刀双掷_1_控制1输入1 ;

  ALU alu_1 (
    .\输入数1第1位 (out_4), .\输入数1第2位 (out_5), .\输入数1第3位 (out_6), .\输入数1第4位 (out_7), .\输入数1第5位 (out_8),
    .\输入数1第6位 (out_9), .\输入数1第7位 (out_10), .\输入数1第8位 (out_11), .\输入数2第1位 (1'b0), .\输入数2第2位 (1'b0),
    .\输入数2第3位 (1'b0), .\输入数2第4位 (1'b0), .\输入数2第5位 (\n2to1单刀双掷_1_控制1输入1 [4]),
    .\输入数2第6位 (\n2to1单刀双掷_1_控制1输入1 [5]), .\输入数2第7位 (\n2to1单刀双掷_1_控制1输入1 [6]),
    .\输入数2第8位 (\n2to1单刀双掷_1_控制1输入1 [7]), .\状态码1 (pc_rom_ir_1_out_12[0]), .\状态码2 (pc_rom_ir_1_out_12[1]),
    .\状态码3 (pc_rom_ir_1_out_12[2]), .\状态码4 (pc_rom_ir_1_out_12[3]), .out_21(alu_1_out_21),
    .out_22(alu_1_out_22), .out_23(alu_1_out_23), .out_24(alu_1_out_24), .out_25(alu_1_out_25),
    .out_26(alu_1_out_26), .out_27(alu_1_out_27), .out_28(alu_1_out_28));
  PC_ROM_IR pc_rom_ir_1 (
    .\时钟信号 (\时钟信号 ), .\写使能信号 (\写使能信号 ), .\RST信号 (\RST信号 ), .in_4(1'b0), .in_5(1'b0), .in_6(1'b0),
    .in_7(1'b0), .in_8(\n2to1单刀双掷_1_控制1输入1 [4]), .in_9(\n2to1单刀双掷_1_控制1输入1 [5]),
    .in_10(\n2to1单刀双掷_1_控制1输入1 [6]), .in_11(\n2to1单刀双掷_1_控制1输入1 [7]), .out_12(pc_rom_ir_1_out_12[0]),
    .out_13(pc_rom_ir_1_out_12[1]), .out_14(pc_rom_ir_1_out_12[2]), .out_15(pc_rom_ir_1_out_12[3]),
    .out_16(pc_rom_ir_1_out_16), .out_17(pc_rom_ir_1_out_17), .out_18(pc_rom_ir_1_out_18),
    .out_19(pc_rom_ir_1_out_19));
  \_8位单刀双掷开关  \u_8位单刀双掷开关_1  (
    .\控制信号 (\RST信号 ), .in_2(alu_1_out_21), .in_3(alu_1_out_22), .in_4(alu_1_out_23), .in_5(alu_1_out_24),
    .in_6(alu_1_out_25), .in_7(alu_1_out_26), .in_8(alu_1_out_27), .in_9(alu_1_out_28),
    .out_10(\n8位单刀双掷开关_1_out_10 ), .out_11(\n8位单刀双掷开关_1_out_11 ), .out_12(\n8位单刀双掷开关_1_out_12 ),
    .out_13(\n8位单刀双掷开关_1_out_13 ), .out_14(\n8位单刀双掷开关_1_out_14 ), .out_15(\n8位单刀双掷开关_1_out_15 ),
    .out_16(\n8位单刀双掷开关_1_out_16 ), .out_17(\n8位单刀双掷开关_1_out_17 ));
  \_2to1单刀双掷  \u_2to1单刀双掷_1  (
    .\控制信号 (\RST信号 ), .\输入1 (1'b0), .\输入2 (pc_rom_ir_1_out_16), .\控制1输入1 (\n2to1单刀双掷_1_控制1输入1 [4]),
    .\控制0输入2 (\n2to1单刀双掷_1_控制1输入1 [4]));
  \_2to1单刀双掷  \u_2to1单刀双掷_2  (
    .\控制信号 (\RST信号 ), .\输入1 (1'b0), .\输入2 (pc_rom_ir_1_out_17), .\控制1输入1 (\n2to1单刀双掷_1_控制1输入1 [5]),
    .\控制0输入2 (\n2to1单刀双掷_1_控制1输入1 [5]));
  // _2to1单刀双掷 2to1单刀双掷_3: pin names not known; wires that end beside it: \RST信号 , 1'b0, pc_rom_ir_1_out_18, \n2to1单刀双掷_1_控制1输入1 [6], \n2to1单刀双掷_1_控制1输入1 [6], \n2to1单刀双掷_1_控制1输入1 [7]
  \_2to1单刀双掷  \u_2to1单刀双掷_4  (
    .\控制信号 (\RST信号 ), .\输入1 (1'b0), .\输入2 (pc_rom_ir_1_out_19), .\控制1输入1 (\n2to1单刀双掷_1_控制1输入1 [7]),
    .\控制0输入2 (\n2to1单刀双掷_1_控制1输入1 [7]));
  \_8位寄存器  \u_8位寄存器_1  (
    .\时钟输入 (\时钟信号 ), .\输入0 (\n8位单刀双掷开关_1_out_10 ), .\输入1 (\n8位单刀双掷开关_1_out_11 ),
    .\输入2 (\n8位单刀双掷开关_1_out_12 ), .\输入3 (\n8位单刀双掷开关_1_out_13 ), .\输入4 (\n8位单刀双掷开关_1_out_14 ),
    .\输入5 (\n8位单刀双掷开关_1_out_15 ), .\输入6 (\n8位单刀双掷开关_1_out_16 ), .\输入7 (\n8位单刀双掷开关_1_out_17 ),
    .\写使能信号 (\写使能信号 ), .\RST信号 (\RST信号 ), .\输出0 (out_4), .\输出1 (out_5), .\输出2 (out_6), .\输出3 (out_7),
    .\输出4 (out_8), .\输出5 (out_9), .\输出6 (out_10), .\输出7 (out_11));
endmodule
