// Logisim project 8位寄存器.circ as structural Verilog: 1 circuit, main circuit 8位寄存器
module \_8位寄存器  (
  input  \时钟输入 ,
  input  \输入0 ,
  input  \输入1 ,
  input  \输入2 ,
  input  \输入3 ,
  input  \输入4 ,
  input  \输入5 ,
  input  \输入6 ,
  input  \输入7 ,
  input  \写使能信号 ,
  input  \RST信号 ,
  output \输出0 ,
  output \输出1 ,
  output \输出2 ,
  output \输出3 ,
  output \输出4 ,
  output \输出5 ,
  output \输出6 ,
  output \输出7 
);

  wire \n2to1单刀双掷_1_控制1输入1 , \n2to1单刀双掷_2_控制1输入1 , \n2to1单刀双掷_3_控制1输入1 , \n2to1单刀双掷_4_控制1输入1 ,
       \n2to1单刀双掷_5_控制1输入1 , \n2to1单刀双掷_6_控制1输入1 , \n2to1单刀双掷_7_控制1输入1 , \n2to1单刀双掷_8_控制1输入1 ,
       \n2选1选择器_1_输出 , \n2选1选择器_2_输出 , \n2选1选择器_3_输出 , \n2选1选择器_4_输出 , \n2选1选择器_5_输出 , \n2选1选择器_6_输出 ,
       \n2选1选择器_7_输出 , \n2选1选择器_8_输出 ;

  \_2选1选择器  \u_2选1选择器_1  (
    .\输入1 (\输入0 ), .\输入2 (\n2to1单刀双掷_1_控制1输入1 ), .\选择_1表示输入1_0表示输入2 (\写使能信号 ), .\输出 (\n2选1选择器_1_输出 ));
  \_2选1选择器  \u_2选1选择器_2  (
    .\输入1 (\输入1 ), .\输入2 (\n2to1单刀双掷_2_控制1输入1 ), .\选择_1表示输入1_0表示输入2 (\写使能信号 ), .\输出 (\n2选1选择器_2_输出 ));
  \_2选1选择器  \u_2选1选择器_3  (
    .\输入1 (\输入2 ), .\输入2 (\n2to1单刀双掷_3_控制1输入1 ), .\选择_1表示输入1_0表示输入2 (\写使能信号 ), .\输出 (\n2选1选择器_3_输出 ));
  \_2选1选择器  \u_2选1选择器_4  (
    .\输入1 (\输入3 ), .\输入2 (\n2to1单刀双掷_4_控制1输入1 ), .\选择_1表示输入1_0表示输入2 (\写使能信号 ), .\输出 (\n2选1选择器_4_输出 ));
  \_2选1选择器  \u_2选1选择器_5  (
    .\输入1 (\输入4 ), .\输入2 (\n2to1单刀双掷_5_控制1输入1 ), .\选择_1表示输入1_0表示输入2 (\写使能信号 ), .\输出 (\n2选1选择器_5_输出 ));
  \_2选1选择器  \u_2选1选择器_6  (
    .\输入1 (\输入5 ), .\输入2 (\n2to1单刀双掷_6_控制1输入1 ), .\选择_1表示输入1_0表示输入2 (\写使能信号 ), .\输出 (\n2选1选择器_6_输出 ));
  \_2选1选择器  \u_2选1选择器_7  (
    .\输入1 (\输入6 ), .\输入2 (\n2to1单刀双掷_7_控制1输入1 ), .\选择_1表示输入1_0表示输入2 (\写使能信号 ), .\输出 (\n2选1选择器_7_输出 ));
  \_2选1选择器  \u_2选1选择器_8  (
    .\输入1 (\输入7 ), .\输入2 (\n2to1单刀双掷_8_控制1输入1 ), .\选择_1表示输入1_0表示输入2 (\写使能信号 ), .\输出 (\n2选1选择器_8_输出 ));
  \_2to1单刀双掷  \u_2to1单刀双掷_1  (
    .\控制信号 (\RST信号 ), .\输入1 (1'b0), .\输入2 (\输出0 ), .\控制1输入1 (\n2to1单刀双掷_1_控制1输入1 ),
    .\控制0输入2 (\n2to1单刀双掷_1_控制1输入1 ));
  \触发器  \u_触发器_1  (.\时钟输入 (\时钟输入 ), .\输入 (\n2选1选择器_1_输出 ), .\触发器的输出Q (\输出0 ));
  \_2to1单刀双掷  \u_2to1单刀双掷_2  (
    .\控制信号 (\RST信号 ), .\输入1 (1'b0), .\输入2 (\输出1 ), .\控制1输入1 (\n2to1单刀双掷_2_控制1输入1 ),
    .\控制0输入2 (\n2to1单刀双掷_2_控制1输入1 ));
  \触发器  \u_触发器_2  (.\时钟输入 (\时钟输入 ), .\输入 (\n2选1选择器_2_输出 ), .\触发器的输出Q (\输出1 ));
  \_2to1单刀双掷  \u_2to1单刀双掷_3  (
    .\控制信号 (\RST信号 ), .\输入1 (1'b0), .\输入2 (\输出2 ), .\控制1输入1 (\n2to1单刀双掷_3_控制1输入1 ),
    .\控制0输入2 (\n2to1单刀双掷_3_控制1输入1 ));
  \触发器  \u_触发器_3  (.\时钟输入 (\时钟输入 ), .\输入 (\n2选1选择器_3_输出 ), .\触发器的输出Q (\输出2 ));
  \_2to1单刀双掷  \u_2to1单刀双掷_4  (
    .\控制信号 (\RST信号 ), .\输入1 (1'b0), .\输入2 (\输出3 ), .\控制1输入1 (\n2to1单刀双掷_4_控制1输入1 ),
    .\控制0输入2 (\n2to1单刀双掷_4_控制1输入1 ));
  \触发器  \u_触发器_4  (.\时钟输入 (\时钟输入 ), .\输入 (\n2选1选择器_4_输出 ), .\触发器的输出Q (\输出3 ));
  \_2to1单刀双掷  \u_2to1单刀双掷_5  (
    .\控制信号 (\RST信号 ), .\输入1 (1'b0), .\输入2 (\输出4 ), .\控制1输入1 (\n2to1单刀双掷_5_控制1输入1 ),
    .\控制0输入2 (\n2to1单刀双掷_5_控制1输入1 ));
  \触发器  \u_触发器_5  (.\时钟输入 (\时钟输入 ), .\输入 (\n2选1选择器_5_输出 ), .\触发器的输出Q (\输出4 ));
  \_2to1单刀双掷  \u_2to1单刀双掷_6  (
    .\控制信号 (\RST信号 ), .\输入1 (1'b0), .\输入2 (\输出5 ), .\控制1输入1 (\n2to1单刀双掷_6_控制1输入1 ),
    .\控制0输入2 (\n2to1单刀双掷_6_控制1输入1 ));
  \触发器  \u_触发器_6  (.\时钟输入 (\时钟输入 ), .\输入 (\n2选1选择器_6_输出 ), .\触发器的输出Q (\输出5 ));
  \触发器  \u_触发器_7  (.\时钟输入 (\时钟输入 ), .\输入 (\n2选1选择器_7_输出 ), .\触发器的输出Q (\输出6 ));
  \触发器  \u_触发器_8  (.\时钟输入 (\时钟输入 ), .\输入 (\n2选1选择器_8_输出 ), .\触发器的输出Q (\输出7 ));
  \_2to1单刀双掷  \u_2to1单刀双掷_7  (
    .\控制信号 (\RST信号 ), .\输入1 (1'b0), .\输入2 (\输出6 ), .\控制1输入1 (\n2to1单刀双掷_7_控制1输入1 ),
    .\控制0输入2 (\n2to1单刀双掷_7_控制1输入1 ));
  \_2to1单刀双掷  \u_2to1单刀双掷_8  (
    .\控制信号 (\RST信号 ), .\输入1 (1'b0), .\输入2 (\输出7 ), .\控制1输入1 (\n2to1单刀双掷_8_控制1输入1 ),
    .\控制0输入2 (\n2to1单刀双掷_8_控制1输入1 ));
endmodule
