// Logisim project D触发器.circ as structural Verilog: 1 circuit, main circuit 触发器
module \触发器  (
  input  \时钟输入 ,
  input  \输入 ,
  output \触发器的输出Q 
);

  wire inverter_1_output, \主锁存器_输出q ;

  Inverter inverter_1 (.Input(\时钟输入 ), .Output(inverter_1_output));
  \D锁存器  \u_主锁存器  (.\时钟输入 (\时钟输入 ), .\输入D (\输入 ), .\输出Q (\主锁存器_输出q ));
  \D锁存器  \u_从锁存器  (.\时钟输入 (inverter_1_output), .\输入D (\主锁存器_输出q ), .\输出Q (\触发器的输出Q ));
endmodule
