// Logisim project D锁存器.circ as structural Verilog: 1 circuit, main circuit 反向输出D锁存器
// D锁存器
module \反向输出D锁存器  (
  input  \时钟输入 ,
  input  \输入D ,
  output \输出Q 
);

  wire INV2_output, inverter_1_output, \TG1_输出 ;

  \传输门  TG1 (.\时钟输入 (\时钟输入 ), .\输入 (\输入D ), .\输出 (\TG1_输出 ));
  Inverter INV1 (.Input(\TG1_输出 ), .Output(\输出Q ));
  Inverter INV2 (.Input(\输出Q ), .Output(INV2_output));
  Inverter inverter_1 (.Input(\时钟输入 ), .Output(inverter_1_output));
  \传输门  TG2 (.\时钟输入 (inverter_1_output), .\输入 (INV2_output), .\输出 (\TG1_输出 ));
endmodule
