// Logisim project SR锁存器.circ as structural Verilog: 1 circuit, main circuit SR锁存器
module \SR锁存器  (
  input  in_1,
  input  in_2
);

  wire nor_1_out, nor_2_out;

  nor nor_1 (nor_1_out, in_1, nor_2_out);
  nor nor_2 (nor_2_out, nor_1_out, in_2);
endmodule
