// Logisim project 传输门.circ as structural Verilog: 1 circuit, main circuit 传输门
module \传输门  (
  input  \时钟输入 ,
  input  \输入 ,
  output \输出 
);

  wire inverter_1_output;

  Inverter inverter_1 (.Input(\时钟输入 ), .Output(inverter_1_output));
  Transistor transistor_1 (.in(\输入 ), .out(\输出 ), .gate(inverter_1_output));
  Transistor #(.\type ("n")) transistor_2 (.in(\输入 ), .out(\输出 ), .gate(\时钟输入 ));
endmodule
