// Logisim project 正在搭建的ROM+IR.circ as structural Verilog: 1 circuit, main circuit PC+ROM+IR
module PC_ROM_IR (
  input  \时钟信号 ,
  input  \写使能信号 ,
  input  \RST信号 ,
  input  in_4,
  input  in_5,
  input  in_6,
  input  in_7,
  input  in_8,
  input  in_9,
  input  in_10,
  input  in_11,
  output out_12,
  output out_13,
  output out_14,
  output out_15,
  output out_16,
  output out_17,
  output out_18,
  output out_19
);

  wire inverter_1_output, inverter_2_output, \n2to1单刀双掷_1_控制1输入1 , \n4位与门_1_输出 ;
  wire [7:0] \pc_1_输出7 , rom_1_data;

  \_2to1单刀双掷  \u_2to1单刀双掷_1  (
    .\控制信号 (\RST信号 ), .\输入1 (1'b0), .\输入2 (\n4位与门_1_输出 ), .\控制1输入1 (\n2to1单刀双掷_1_控制1输入1 ),
    .\控制0输入2 (\n2to1单刀双掷_1_控制1输入1 ));
  Inverter inverter_1 (.Input(\时钟信号 ), .Output(inverter_1_output));
  PC pc_1 (
    .\时钟信号 (\时钟信号 ), .\写使能信号 (1'b1), .\RST信号 (\RST信号 ), .\地址输入0 (in_4), .\地址输入1 (in_5), .\地址输入2 (in_6),
    .\地址输入3 (in_7), .\地址输入4 (in_8), .\地址输入5 (in_9), .\地址输入6 (in_10), .\地址输入7 (in_11),
    .PC_Src(\n2to1单刀双掷_1_控制1输入1 ), .\输出0 (\pc_1_输出7 [7]), .\输出1 (\pc_1_输出7 [6]), .\输出2 (\pc_1_输出7 [5]),
    .\输出3 (\pc_1_输出7 [4]), .\输出4 (\pc_1_输出7 [3]), .\输出5 (\pc_1_输出7 [2]), .\输出6 (\pc_1_输出7 [1]),
    .\输出7 (\pc_1_输出7 [0]));
  ROM rom_1 (.addr(\pc_1_输出7 ), .data(rom_1_data), .sel(1'b1));
  \_8位寄存器  IR (
    .\时钟输入 (inverter_1_output), .\输入0 (rom_1_data[7]), .\输入1 (rom_1_data[6]), .\输入2 (rom_1_data[5]),
    .\输入3 (rom_1_data[4]), .\输入4 (rom_1_data[3]), .\输入5 (rom_1_data[2]), .\输入6 (rom_1_data[1]),
    .\输入7 (rom_1_data[0]), .\写使能信号 (\写使能信号 ), .\RST信号 (\RST信号 ), .\输出0 (out_12), .\输出1 (out_13),
    .\输出2 (out_14), .\输出3 (out_15), .\输出4 (out_16), .\输出5 (out_17), .\输出6 (out_18), .\输出7 (out_19));
  Inverter inverter_2 (.Input(out_14), .Output(inverter_2_output));
  \_4位与门  \u_4位与门_1  (
    .\第一位输入 (out_12), .\第二位输入 (out_13), .\第三位输入 (inverter_2_output), .\第四位输入 (out_15), .\输出 (\n4位与门_1_输出 ));

  // Notes on the sheet:
  //   contents of rom_1 (hex, n*v repeats v):
  //   e1 2 13 42 51 60 70 20 30 80 90 a0 b5 c3 f0 d0 1 2 3 4 5 6 7 8 9 a b c d e f
endmodule
