// Logisim project 程序计数器PC.circ as structural Verilog: 1 circuit, main circuit PC
module PC (
  input  \时钟信号 ,
  input  \写使能信号 ,
  input  \RST信号 ,
  input  \地址输入0 ,
  input  \地址输入1 ,
  input  \地址输入2 ,
  input  \地址输入3 ,
  input  \地址输入4 ,
  input  \地址输入5 ,
  input  \地址输入6 ,
  input  \地址输入7 ,
  input  PC_Src,
  output \输出0 ,
  output \输出1 ,
  output \输出2 ,
  output \输出3 ,
  output \输出4 ,
  output \输出5 ,
  output \输出6 ,
  output \输出7 
);

  wire \八位数加法器_1_out_17 , \八位数加法器_1_out_18 , \八位数加法器_1_out_19 , \八位数加法器_1_out_20 , \八位数加法器_1_out_21 ,
       \八位数加法器_1_out_22 , \八位数加法器_1_out_23 , \八位数加法器_1_out_24 ;
  wire [7:0] \_0_PC_1_1_跳转地址_out_18 , \n2to1单刀双掷_1_控制1输入1 ;

  \_8位寄存器  \u_8位寄存器_1  (
    .\时钟输入 (\时钟信号 ), .\输入0 (\_0_PC_1_1_跳转地址_out_18 [0]), .\输入1 (\_0_PC_1_1_跳转地址_out_18 [1]),
    .\输入2 (\_0_PC_1_1_跳转地址_out_18 [2]), .\输入3 (\_0_PC_1_1_跳转地址_out_18 [3]),
    .\输入4 (\_0_PC_1_1_跳转地址_out_18 [4]), .\输入5 (\_0_PC_1_1_跳转地址_out_18 [5]),
    .\输入6 (\_0_PC_1_1_跳转地址_out_18 [6]), .\输入7 (\_0_PC_1_1_跳转地址_out_18 [7]), .\写使能信号 (\写使能信号 ),
    .\RST信号 (\RST信号 ), .\输出0 (\输出0 ), .\输出1 (\输出1 ), .\输出2 (\输出2 ), .\输出3 (\输出3 ), .\输出4 (\输出4 ),
    .\输出5 (\输出5 ), .\输出6 (\输出6 ), .\输出7 (\输出7 ));
  \八位数加法器  \u_八位数加法器_1  (
    .\加数1的第1位 (\输出0 ), .\加数1的第2位 (\输出1 ), .\加数1的第3位 (\输出2 ), .\加数1的第4位 (\输出3 ), .\加数1的第5位 (\输出4 ),
    .\加数1的第6位 (\输出5 ), .\加数1的第7位 (\输出6 ), .\加数1的第8位 (\输出7 ), .\加数2的第1位 (1'b0), .\加数2的第2位 (1'b0),
    .\加数2的第3位 (1'b0), .\加数2的第4位 (1'b0), .\加数2的第5位 (1'b0), .\加数2的第6位 (1'b0), .\加数2的第7位 (1'b0),
    .\加数2的第8位 (1'b1), .out_17(\八位数加法器_1_out_17 ), .out_18(\八位数加法器_1_out_18 ), .out_19(\八位数加法器_1_out_19 ),
    .out_20(\八位数加法器_1_out_20 ), .out_21(\八位数加法器_1_out_21 ), .out_22(\八位数加法器_1_out_22 ),
    .out_23(\八位数加法器_1_out_23 ), .out_24(\八位数加法器_1_out_24 ));  // open: cout
  \_2to1单刀双掷  \u_2to1单刀双掷_1  (
    .\控制信号 (\RST信号 ), .\输入1 (\RST信号 ), .\输入2 (\八位数加法器_1_out_17 ), .\控制1输入1 (\n2to1单刀双掷_1_控制1输入1 [0]),
    .\控制0输入2 (\n2to1单刀双掷_1_控制1输入1 [0]));
  \_2to1单刀双掷  \u_2to1单刀双掷_2  (
    .\控制信号 (\RST信号 ), .\输入1 (\RST信号 ), .\输入2 (\八位数加法器_1_out_18 ), .\控制1输入1 (\n2to1单刀双掷_1_控制1输入1 [1]),
    .\控制0输入2 (\n2to1单刀双掷_1_控制1输入1 [1]));
  \_2to1单刀双掷  \u_2to1单刀双掷_3  (
    .\控制信号 (\RST信号 ), .\输入1 (\RST信号 ), .\输入2 (\八位数加法器_1_out_19 ), .\控制1输入1 (\n2to1单刀双掷_1_控制1输入1 [2]),
    .\控制0输入2 (\n2to1单刀双掷_1_控制1输入1 [2]));
  \_2to1单刀双掷  \u_2to1单刀双掷_4  (
    .\控制信号 (\RST信号 ), .\输入1 (\RST信号 ), .\输入2 (\八位数加法器_1_out_20 ), .\控制1输入1 (\n2to1单刀双掷_1_控制1输入1 [3]),
    .\控制0输入2 (\n2to1单刀双掷_1_控制1输入1 [3]));
  \_2to1单刀双掷  \u_2to1单刀双掷_5  (
    .\控制信号 (\RST信号 ), .\输入1 (\RST信号 ), .\输入2 (\八位数加法器_1_out_21 ), .\控制1输入1 (\n2to1单刀双掷_1_控制1输入1 [4]),
    .\控制0输入2 (\n2to1单刀双掷_1_控制1输入1 [4]));
  \_2to1单刀双掷  \u_2to1单刀双掷_6  (
    .\控制信号 (\RST信号 ), .\输入1 (\RST信号 ), .\输入2 (\八位数加法器_1_out_22 ), .\控制1输入1 (\n2to1单刀双掷_1_控制1输入1 [5]),
    .\控制0输入2 (\n2to1单刀双掷_1_控制1输入1 [5]));
  \_2to1单刀双掷  \u_2to1单刀双掷_7  (
    .\控制信号 (\RST信号 ), .\输入1 (\RST信号 ), .\输入2 (\八位数加法器_1_out_23 ), .\控制1输入1 (\n2to1单刀双掷_1_控制1输入1 [6]),
    .\控制0输入2 (\n2to1单刀双掷_1_控制1输入1 [6]));
  \_2to1单刀双掷  \u_2to1单刀双掷_8  (
    .\控制信号 (\RST信号 ), .\输入1 (\RST信号 ), .\输入2 (\八位数加法器_1_out_24 ), .\控制1输入1 (\n2to1单刀双掷_1_控制1输入1 [7]),
    .\控制0输入2 (\n2to1单刀双掷_1_控制1输入1 [7]));
  \_8位2选1选择器  \_0_PC_1_1_跳转地址  (
    .\输入1第1位 (\地址输入0 ), .\输入1第2位 (\地址输入1 ), .\输入1第3位 (\地址输入2 ), .\输入1第4位 (\地址输入3 ), .\输入1第5位 (\地址输入4 ),
    .\输入1第6位 (\地址输入5 ), .\输入1第7位 (\地址输入6 ), .\输入1第8位 (\地址输入7 ), .\输入2第1位 (\n2to1单刀双掷_1_控制1输入1 [0]),
    .\输入2第2位 (\n2to1单刀双掷_1_控制1输入1 [1]), .\输入2第3位 (\n2to1单刀双掷_1_控制1输入1 [2]),
    .\输入2第4位 (\n2to1单刀双掷_1_控制1输入1 [3]), .\输入2第5位 (\n2to1单刀双掷_1_控制1输入1 [4]),
    .\输入2第6位 (\n2to1单刀双掷_1_控制1输入1 [5]), .\输入2第7位 (\n2to1单刀双掷_1_控制1输入1 [6]),
    .\输入2第8位 (\n2to1单刀双掷_1_控制1输入1 [7]), .\操控码 (PC_Src), .out_18(\_0_PC_1_1_跳转地址_out_18 [0]),
    .out_19(\_0_PC_1_1_跳转地址_out_18 [1]), .out_20(\_0_PC_1_1_跳转地址_out_18 [2]),
    .out_21(\_0_PC_1_1_跳转地址_out_18 [3]), .out_22(\_0_PC_1_1_跳转地址_out_18 [4]),
    .out_23(\_0_PC_1_1_跳转地址_out_18 [5]), .out_24(\_0_PC_1_1_跳转地址_out_18 [6]),
    .out_25(\_0_PC_1_1_跳转地址_out_18 [7]));
endmodule
