// Logisim project 递增器1.circ as structural Verilog: 1 circuit, main circuit 递增器
module \递增器  (
  input  \时钟信号 ,
  input  \使写能信号 ,
  input  \RST信号 ,
  input  in_4,
  input  in_5,
  input  in_6,
  input  in_7,
  input  in_8,
  input  in_9,
  input  in_10,
  input  in_11,
  input  \控制码1 ,
  input  \控制码2 ,
  input  \控制码3 ,
  input  \控制码4 ,
  output out_16,
  output out_17,
  output out_18,
  output out_19,
  output out_20,
  output out_21,
  output out_22,
  output out_23
);

  wire alu_1_out_21, alu_1_out_22, alu_1_out_23, alu_1_out_24, alu_1_out_25, alu_1_out_26, alu_1_out_27,
       alu_1_out_28;
  wire [7:0] \n2to1单刀双掷_1_控制1输入1 ;

  \_8位寄存器  \u_8位寄存器_1  (
    .\时钟输入 (\时钟信号 ), .\输入0 (\n2to1单刀双掷_1_控制1输入1 [0]), .\输入1 (\n2to1单刀双掷_1_控制1输入1 [1]),
    .\输入2 (\n2to1单刀双掷_1_控制1输入1 [2]), .\输入3 (\n2to1单刀双掷_1_控制1输入1 [3]), .\输入4 (\n2to1单刀双掷_1_控制1输入1 [4]),
    .\输入5 (\n2to1单刀双掷_1_控制1输入1 [5]), .\输入6 (\n2to1单刀双掷_1_控制1输入1 [6]), .\输入7 (\n2to1单刀双掷_1_控制1输入1 [7]),
    .\写使能信号 (\使写能信号 ), .\RST信号 (\RST信号 ), .\输出0 (out_16), .\输出1 (out_17), .\输出2 (out_18), .\输出3 (out_19),
    .\输出4 (out_20), .\输出5 (out_21), .\输出6 (out_22), .\输出7 (out_23));
  ALU alu_1 (
    .\输入数1第1位 (out_16), .\输入数1第2位 (out_17), .\输入数1第3位 (out_18), .\输入数1第4位 (out_19), .\输入数1第5位 (out_20),
    .\输入数1第6位 (out_21), .\输入数1第7位 (out_22), .\输入数1第8位 (out_23), .\输入数2第1位 (in_4), .\输入数2第2位 (in_5),
    .\输入数2第3位 (in_6), .\输入数2第4位 (in_7), .\输入数2第5位 (in_8), .\输入数2第6位 (in_9), .\输入数2第7位 (in_10),
    .\输入数2第8位 (in_11), .\状态码1 (\控制码1 ), .\状态码2 (\控制码2 ), .\状态码3 (\控制码3 ), .\状态码4 (\控制码4 ),
    .out_21(alu_1_out_21), .out_22(alu_1_out_22), .out_23(alu_1_out_23), .out_24(alu_1_out_24),
    .out_25(alu_1_out_25), .out_26(alu_1_out_26), .out_27(alu_1_out_27), .out_28(alu_1_out_28));
  \_2to1单刀双掷  \u_2to1单刀双掷_1  (
    .\控制信号 (\RST信号 ), .\输入1 (1'b0), .\输入2 (alu_1_out_21), .\控制1输入1 (\n2to1单刀双掷_1_控制1输入1 [0]),
    .\控制0输入2 (\n2to1单刀双掷_1_控制1输入1 [0]));
  \_2to1单刀双掷  \u_2to1单刀双掷_2  (
    .\控制信号 (\RST信号 ), .\输入1 (1'b0), .\输入2 (alu_1_out_22), .\控制1输入1 (\n2to1单刀双掷_1_控制1输入1 [1]),
    .\控制0输入2 (\n2to1单刀双掷_1_控制1输入1 [1]));
  \_2to1单刀双掷  \u_2to1单刀双掷_3  (
    .\控制信号 (\RST信号 ), .\输入1 (1'b0), .\输入2 (alu_1_out_23), .\控制1输入1 (\n2to1单刀双掷_1_控制1输入1 [2]),
    .\控制0输入2 (\n2to1单刀双掷_1_控制1输入1 [2]));
  \_2to1单刀双掷  \u_2to1单刀双掷_4  (
    .\控制信号 (\RST信号 ), .\输入1 (1'b0), .\输入2 (alu_1_out_24), .\控制1输入1 (\n2to1单刀双掷_1_控制1输入1 [3]),
    .\控制0输入2 (\n2to1单刀双掷_1_控制1输入1 [3]));
  \_2to1单刀双掷  \u_2to1单刀双掷_5  (
    .\控制信号 (\RST信号 ), .\输入1 (1'b0), .\输入2 (alu_1_out_25), .\控制1输入1 (\n2to1单刀双掷_1_控制1输入1 [4]),
    .\控制0输入2 (\n2to1单刀双掷_1_控制1输入1 [4]));
  \_2to1单刀双掷  \u_2to1单刀双掷_6  (
    .\控制信号 (\RST信号 ), .\输入1 (1'b0), .\输入2 (alu_1_out_26), .\控制1输入1 (\n2to1单刀双掷_1_控制1输入1 [5]),
    .\控制0输入2 (\n2to1单刀双掷_1_控制1输入1 [5]));
  \_2to1单刀双掷  \u_2to1单刀双掷_7  (
    .\控制信号 (\RST信号 ), .\输入1 (1'b0), .\输入2 (alu_1_out_27), .\控制1输入1 (\n2to1单刀双掷_1_控制1输入1 [6]),
    .\控制0输入2 (\n2to1单刀双掷_1_控制1输入1 [6]));
  \_2to1单刀双掷  \u_2to1单刀双掷_8  (
    .\控制信号 (\RST信号 ), .\输入1 (1'b0), .\输入2 (alu_1_out_28), .\控制1输入1 (\n2to1单刀双掷_1_控制1输入1 [7]),
    .\控制0输入2 (\n2to1单刀双掷_1_控制1输入1 [7]));
endmodule
